// Logisim project storage.circ as structural Verilog: 17 circuits, main circuit ◇MIPS Regfile
// 字库
module \字库电路  (
  input  [6:0] \区号 ,
  input  [6:0] \位号 ,
  output [31:0] D0,
  output [31:0] D1,
  output [31:0] D6,
  output [31:0] D3,
  output [31:0] D4,
  output [31:0] D5,
  output [31:0] D6_2,
  output [31:0] D7
);

  wire decoder_1_out0, decoder_1_out1, decoder_1_out2, decoder_1_out3;
  wire [1:0] subtractor_2_out_2;
  wire [6:0] multiplier_1_cout, multiplier_1_out, subtractor_1_out;
  wire [11:0] subtractor_2_out;
  wire [13:0] adder_1_out, bit_extender_1_out;

  Decoder #(.select(2), .enable("false")) decoder_1 (
    .out0(decoder_1_out0), .out1(decoder_1_out1), .out2(decoder_1_out2), .out3(decoder_1_out3),
    .sel(subtractor_2_out_2));
  ROM #(.addrWidth(12), .dataWidth(32)) rom_1 (.addr(subtractor_2_out), .data(D1), .sel(decoder_1_out3));
  ROM #(.addrWidth(14), .dataWidth(32)) rom_2 (.addr({subtractor_2_out_2, subtractor_2_out}), .data(D0));  // open: sel
  ROM #(.addrWidth(14), .dataWidth(32)) rom_3 (.addr({subtractor_2_out_2, subtractor_2_out}), .data(D4));  // open: sel
  Subtractor #(.width(7)) subtractor_1 (.a(\区号 ), .b(7'b0000001), .out(subtractor_1_out));  // open: bin, bout
  Multiplier #(.width(7)) multiplier_1 (
    .a(subtractor_1_out), .b(7'b1011110), .out(multiplier_1_out), .cout(multiplier_1_cout));  // open: cin
  ROM #(.addrWidth(12), .dataWidth(32)) rom_4 (.addr(subtractor_2_out), .data(D1), .sel(decoder_1_out2));
  ROM #(.addrWidth(14), .dataWidth(32)) rom_5 (.addr({subtractor_2_out_2, subtractor_2_out}), .data(D5));  // open: sel
  Adder #(.width(14)) adder_1 (
    .a({multiplier_1_cout, multiplier_1_out}), .b(bit_extender_1_out), .out(adder_1_out));  // open: cin, cout
  assign bit_extender_1_out = {{7{1'b0}}, \位号 };  // Bit_Extender bit_extender_1
  ROM #(.addrWidth(12), .dataWidth(32)) rom_6 (.addr(subtractor_2_out), .data(D1), .sel(decoder_1_out1));
  ROM #(.addrWidth(14), .dataWidth(32)) rom_7 (.addr({subtractor_2_out_2, subtractor_2_out}), .data(D6));  // open: sel
  ROM #(.addrWidth(14), .dataWidth(32)) rom_8 (
    .addr({subtractor_2_out_2, subtractor_2_out}), .data(D6_2));  // open: sel
  Subtractor #(.width(14)) subtractor_2 (
    .a(adder_1_out), .b(14'h1), .out({subtractor_2_out_2, subtractor_2_out}));  // open: bin, bout
  DotMatrix #(.inputtype("row"), .matrixcols(16), .matrixrows(16), .dotshape("circle")) dotmatrix_1 (
    .row0(D0[15:0]), .row1(D0[31:16]), .row2(D1[15:0]), .row3(D1[31:16]), .row4(D6[15:0]), .row5(D6[31:16]),
    .row6(D3[15:0]), .row7(D3[31:16]), .row8(D4[15:0]), .row9(D4[31:16]), .row10(D5[15:0]),
    .row11(D5[31:16]), .row12(D6_2[15:0]), .row13(D6_2[31:16]), .row14(D7[15:0]), .row15(D7[31:16]));
  ROM #(.addrWidth(12), .dataWidth(32)) rom_9 (.addr(subtractor_2_out), .data(D1), .sel(decoder_1_out0));
  ROM #(.addrWidth(14), .dataWidth(32)) rom_10 (.addr({subtractor_2_out_2, subtractor_2_out}), .data(D3));  // open: sel
  ROM #(.addrWidth(14), .dataWidth(32)) rom_11 (.addr({subtractor_2_out_2, subtractor_2_out}), .data(D7));  // open: sel

  // Other names for the same wires on the sheet: D2[31:0] = D6; D6_t[31:0] = D6_2

  // Notes on the sheet:
  //   输入引脚区
  //   输入引脚区
  //   请勿增改引脚，请勿修改子电路封装
  //   片选信号，低电平D输出高阻
  //   contents of rom_2 (hex, n*v repeats v):
  //   8*0 1000000 0 0 2400000 5*0 c0000 18000000 16*0 800000 0 0 0 10040000 7f00000 0 0 80000 800000 0 0 0
  //   c1803e0 0 600000 5*0 200000 0 18200000 180006 c003000 0 0 0 800000 1c00000 1c00000 200000 900000
  //   48003000 0 0 500000 0 40000 1c00000 38300000 800080 800080 3c00000 3c00000 c1803e0 1400080 1c00080 0
  //   0 800000 800000 0 0 0 800000 800000 3ffc0000 16*0 1000000 0 0 800000 5*0 8e00000 4200000 9*0 8080000
  //   8080000 8080000 8480000 5*8080000 11*10080000 10*c1803e0 0 0 5*10080000 11080000 4*10080000 16*0
  //   1800000 6*0 40000 20000000 5*0 20000 4*0 400000 38*0 7f80000 60000000 ff00000 0 0 1000100 26*0
  //   10000c0 800080 400180 0 0 800000 9*0 80000 2000000 2060008 0 60008 200000 30004 0 60008 2000000
  //   2060008 0 100000 800000 860008 0 60008 0 60008 0 30004 800000 830004 0 0 60008 0 30004 0 80000 0 0 0
  //   8000000 0 200000 230004 250002 0 30004 20000 0 100000 0 0 100000 0 f80000 fb0004 fa0000 800000 0
  //   4000000 800000 1000000 0 0 0 200000 0 800000 0 0 0 8000000 5*0 1000000 13*0 1ffe0000 0 3c0000 0
  //   400000 0 0 0 100000 1000000 1060008 2000000 2060008 2000000 2060008 1000000 1060008 0 60008 200000
  //   260008 0 60008 0 60008 0 60008 0 60008 2000000 2060008 0 60008 0 0 60008 0 60008 2000000 2060008 0 0
  //   0 2000000 0 0 60008 40000 0 60008 40000 0 60008 20000 0 60008 40000 0 60008 20000 12*0 400000 400000
  //   4*0 800000 0 0 0 30004 10*0 800000 0 0 800000 6*0 800000 8*0 380000 0 0 0 3e00000 21*0 400000 48*0
  //   800000 5*0 2200000 0 3c00000 0 6300000 38*0 300000 19*0 800000 25*0 800000 4400000 2000000 0 800000
  //   4400000 2000000 0 1000000 4400000 2000000 0 800000 4400000 2000000 0 800000 8800000 2000000 7c00000
  //   1000080 2800440 1000200 0 1000000 0 800000 800000 4400000 2000000 5*0 8000000 4000000 0 0 4000000
  //   1000000 0 1000000 0 0 0 200000 800000 0 1000000 400000 0 0 0 2000000 1000000 10080000 0 1000000 0 0
  //   0 2000000 0 3fe00000 8000000 2000000 0 0 1000000 100000 27*0 1000100 1800180 16*0 1000100 1000100
  //   1800180 1800180 1000100 1000100 1800180 1800180 1000100 1000100 1800180 1000100 1800180 1800180
  //   1000100 1800180 1000100 1000100 1800180 1000100 1800180 1800180 1000100 1800180 8*0 4*1000100
  //   4*1800180 4*1000100 1800180 1000100 1800180 1800180 1800180 1000100 1000100 1800180 1000100 1800180
  //   1800180 1800180 15*0 600000 6*0 80000 10000000 5*0 20000 4*0 200000 38*0 7f80000 60000000 ff00000 0
  //   0 1000100 26*0 400030 800080 1000600 0 600000 6*0 80000 10000000 5*0 20000 4*0 200000 38*0 7f80000
  //   60000000 ff00000 0 0 1000100 26*0 400030 800080 1000600 0 4*300c0ff0 381c0ff0 381c0ff0 300c0ff0
  //   3bdc0ff0 3ffc0ff0 3dfc0ff0 3ffc0ff0 3e7c0ff0 3f7c0ff0 3cfc0ff0 c423c423 2a543bdc 3bdc3bdc d5abc423
  //   294030c 39c030c fd6bfcf3 fce3fdf3 fc3ffe7f 3c00180 3c00180 fc3ffe7f e700420 f18ffbdf 7e00180
  //   f81ffe7f 66003c0 f99ffc3f 7e003c0 f81ffc3f 0 ffffffff 3c00180 1c380000 7e003c0 1800000 381c0ff0
  //   3ffc0ff0 4400000 400000 4000000 1800180 1800180 1800180 c000c0 1800180 1800180 1800180 4*0 1ff80000
  //   8001ffff 0 60002 600060 60004000 6000600 7e0000 700070 7e000000 e000e00 c000c c000c0 0 7000380 0
  //   300c300c 1800000 c000c00 c000c000 30003 0 80008000 10001 0 24001800 10081ff8 1c00000 3800000 4800000
  //   fb7fffff 1000100 38000000 6*0 1c00040 0 1e00060 0 3c001e0 3c000c0 0 0 1b00110 0 7000200 0 3e00120
  //   1e00180 0 0 1800180 0 1800180 0 1800180 1800180 0 0 7e00180 0 1800180 0 7e003c0 5a00180 0 0 3e001e00
  //   0 fc0078 0 1a001e00 ec0078 0 3cb0301 f800e0 0 7d00fe00 40004000 1ff00f0 3ec07580 10000 0 1d781900 0
  //   1800080 0 1df00900 f80098 0 0 2400040 0 2400200 0 4e00200 7700040 0 77fc01f8 12e00c0 0 7000300 0
  //   c8008c0 3c00180 0 1cde0000 1f80078 0 78000800 0 3cc01838 7801c00 0 0 2000200 0 400040 0 2000200
  //   600040 0 0 2000180 0 2000180 0 3000180 0 0 7ff80000 4000000 1000000 1bfe2004 1000000 0 0 1000100 0 0
  //   8000000 0 0 0 10000000 0 800000 0 0 0 800000 7ffc0000 0 1000000 80000 0 ff00020 20*0 7ffc3ffc 7f0000
  //   ff000000 3010301 80c080c0 5*0 ffffffff c000c000 ffffffff 30003 c000c000 30003 ffffffff 0 ffffffff 0
  //   8000ffff 80008000 1ffff 10001 80008000 10001 ffff 112*0 2f7e0004 7ffe0004 10401040 10401040 900090
  //   400040 1040200 10201020 440080 fffe0824 21e02018 4440440 5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
  //   contents of rom_3 (hex, n*v repeats v):
  //   0 0 0 180 0 4100410 c30 4400440 2600030 0 fe61c3 2400240 318c 4*0 400040 1000100 4000800 400020
  //   4800900 1200090 1000100 800080 2800280 500050 8800900 880048 7800700 f00070 800080 1400080 1ff8 0
  //   10040808 4100808 4000200 18181818 10041004 10041004 8000fc0 0 800040 800080 2400240 4000200 20022002
  //   408141c1 1000100 3800540 1ffc0000 3ffc0000 20881104 12042102 12202140 1000080 32006200 380026
  //   21800600 c20030 12242142 1800000 18180000 1c00080 800ff8 0 1000100 4800480 c000c00 9800b0 20022002
  //   19001900 1800180 58c0200 1400220 1352134c 4100808 7f00ff8 20042004 3ffc3ffc 48095005 10042002
  //   1ffc3ffe 20042004 3ffc3ffc 8080808 ff80ff8 2401998 30003c 6001e00 800080 4900080 17*0 3000300
  //   18000c0 6000c0 31801980 600060 18601860 3000300 18600cc0 7e00ce0 1b181b18 c600c60 30c03060 30303060
  //   36603360 30183018 33183318 30403040 331831b0 30f831b8 31981998 21822182 218220c2 20322062 2ff228c2
  //   20322032 26322732 20c22062 26322362 203221f2 44924492 44224422 44424422 44124412 45f24522 44124412
  //   44924492 44224422 44924492 44124412 44524452 40c140c1 418140c1 40314061 4ff144c1 40314031 46314731
  //   40c14061 46314361 40b14371 46d946d9 0 0 40024002 40024002 40024002 4c724a52 42224222 44224462
  //   41024102 44224222 42424242 40824082 0 10080000 800080 2200220 8880888 8500888 3200220 5080508
  //   a140a14 a540a54 8500820 2200140 5080208 a280428 c300c30 0 1800180 0 ff80220 1800180 2180100 cd8058c
  //   0 400040 2000200 1401ffc 800080 0 0 0 2000100 c180c18 1800180 c00060 300060 18c00cc0 300030 c300c30
  //   1800180 c300660 3f00670 30003000 1800 30006000 1ff80000 c0006 8000c0 12341224 7f00430 c0c0c18
  //   18001800 c0c0c0c c000c20 c000c20 183c1800 c180c18 1800180 c000c0 ce00dc0 c000c00 114c134c 8d008d0
  //   180c180c c000fe0 188c180c cc00fe0 180030 1800180 c080c08 6400c20 d680d68 36001c0 1800180 6000300
  //   6000600 6000c0 300030 1004 0 0 7e00060 6180618 c000c00 c600c60 ff00c30 1800180 7800cc0 6300630
  //   1800180 c000c0 7c00660 1800180 18c618c6 c300c30 6300630 6180618 6300630 6000600 1e00300 1800180
  //   c300c30 6200c10 d6808cc 1c00360 3200610 1800060 1000200 0 400020 fe61c3 9b00540 9480550 4000400
  //   8000800 100030 100018 1000080 1000080 c080608 6040504 4440244 4440244 200040 200040 4000c00 4000c00
  //   8100810 8100810 10000000 10000000 200040 200040 4000400 4000400 2800280 2800280 2a00220 2a00220
  //   1c800b80 1c800b80 4000400 4000400 c800b0 c800b0 100008 80008 80008 1000100 1000100 4000300 4000300
  //   4100420 10001000 14040a04 18082c04 12082104 6*10100810 1e00080 1e00080 1e00080 e01180 e01180 e01180
  //   10100810 10100810 10100810 800080 2e201430 16081608 22882104 1c80308 1280604 1240e02 9240924
  //   11221122 400040 400040 2f00200 4200e20 6040388 18202c20 60c0388 c080608 6040504 18040c0c 800140
  //   c019b0 4200620 11*0 2000100 1000180 1000100 800080 200010 100008 800080 800080 2200120 2100110
  //   2080208 2080208 fc000f8 fc000f8 800040 800040 1000080 1000080 80008 80008 2200220 2200220 400020
  //   400020 2200140 2200140 2000200 2000200 400020 400020 800140 800140 1000080 1000080 800040 4*1000080
  //   2000220 2000220 1000080 0 800140 8880490 4000200 10040808 10040808 10040808 2000200 2000200 2000200
  //   1000080 1000080 1000080 201040 201040 201040 10840888 10840888 10840888 2800040 10000000 4100200
  //   1400080 803ffc 800080 1000100 1ff80020 20 100010 40004 400020 4400440 4400440 4400420 8040804 200010
  //   100008 3ffe0880 800080 1000080 400020 100008 1080108 800080 8*0 43007f0 c380c70 c000c00 4300430
  //   c000c20 6000300 c180c18 1a2c1bec 1800180 ce00dc0 4300430 114c134c 8c808c8 41007f0 180c180c c180c18
  //   c000fe0 6000300 1800180 1800180 318c318c 36001c0 18003c0 e301c18 8*0 18c018c0 63006e0 1c00120
  //   c300660 c200600 8000800 6180618 6300630 3000300 66006c0 2200140 c300c30 1200320 2000200 6300630
  //   2400240 d800f60 6300630 3000300 6080608 19303118 2200140 19301110 1d5c194c 38*0 43007f0 c380c70
  //   c380c70 c000c00 8300430 c000c20 c200fe0 db00ff0 380070 d180c98 c980c98 c600cc0 8300430 114c134c
  //   c180c18 180c180c c180c18 c000fe0 18001800 1800180 3600320 318c318c 36001c0 c180c18 3d80678 318c318c
  //   318c318c 6180730 18d81d98 6180730 c000c 1b061b06 31803d8 15*0 c2006e0 6300630 6300660 6000600
  //   8600460 6080c00 40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
  //   输出引脚区
  //   电路功能：利用下图中给定的ROM器件实现汉字16*16点阵字库文件，不允许修改ROM地址数据位宽，字库数据可以通过参考字库导出
  //   代替下方的空白电路
  //   用上方的4块ROM进行扩展
  //   contents of rom_4 (hex, n*v repeats v):
  //   18c618c6 4cc03fe 7fcc00ce 7ff800ac 2cff7f8e e1affff 7ffe0cc2 7ffe4862 19987f98 7ffe0186 fffc03ff
  //   7fff0238 3a781830 1bfe1ede ffc0c0c 7fff0332 19ff0982 183018fe ffc0c0c ffc0c0c 198c1d8e d180c18
  //   1b7e13de 14781fff 14701fff 1818181f 359919f9 7f7f7f60 1f8c1fee 189408d8 3d8831fc e6d0c6c 1830194e
  //   7fff0032 6f267bfc 7ffe4434 c21ffe 6fc038f 7c1c007e 4e000fe 10e318e3 7dff40d8 194c33fe 19b319ff
  //   2d3a7ff6 7fff0662 ffdf325a 5e1073ff 41fe7fd2 ff8c0c0c c83fff 7fff0662 35eb1bff 1e3e1034 1b0c1bfe
  //   5fc007e 7f000ff 18331cff 1800ff0 ff004f0 7e320020 7fff0102 53e03fe 4600060 3afc18bf 1fff1821
  //   19ff1032 330c3f3e 7fff0232 6f67ef7 19731bff 7e0c44fe 1cf014f0 4ba00fe 3a5f1c5a 19041bff 4300030
  //   7ff0032 271a7fff 183ff8 30ff38b2 30e21c60 7fff0ce2 7fff0182 7fff0602 24180018 198319ff c080c0c
  //   d0e0c0c 77e0676 7600380 8320c20 1ffe1064 8301838 197a1878 10302030 7ffc0a68 1a6433fe 7ed805fe
  //   1bff1032 35cc19ff 70b03ff 5ff0132 8660dff 63c7fac 2cba7ff6 18061ffc 2d997dff 6c667fe6 32fd38ff
  //   1c203bc fefc00cc fff0831 28703fff 8c903f1 78fe1cc6 7e324030 1bff18ec 1a001bff 3eff24c2 3f7e1b36
  //   14701fff 7fff0662 318c398e fefc0068 35fa39e8 feff0042 19ff18f2 7e47427c 18f618f7 5f000fe 1b0013fe
  //   36c837cc 3a0c1cfe 19fe0d64 189b1d19 24227e30 fff60c37 2000380 18fe1064 37303ffc ff03ffe 0 c7000f00
  //   16*0 79830701 1500f987 1e011500
  //   contents of rom_5 (hex, n*v repeats v):
  //   0 18002000 30000000 0 0 2200220 0 8800880 c001c0 0 38 2400240 5*0 400040 1000100 1000200 1000080
  //   2400480 2400120 1000100 800080 2800280 500050 8400880 1080088 7c00780 1f000f0 80 4100220 1800000
  //   1800000 20021004 2200410 8040400 18181818 10041004 10041004 4000800 18180000 3b001080 800080 4800480
  //   1ff80800 0 20022002 1000100 1000100 0 3ffc0000 70 c18 c1c 1001ffc 3000e00 1a00060 6181860 c30030c
  //   c18 3c003c0 3c3c3c3c 2200220 800080 0 0 0 6080c00 cb01898 10041004 a081900 7800100 12520a52 400080
  //   11d21152 9480888 f780ff8 10081008 1ff81ff8 2632280a 4100808 7f00ff8 20042004 3ffc3ffc 10041004
  //   1ffc1ffc 9900420 40 100 800080 3e003e0 3ffc0000 16*0 3000300 6200300 18600060 1803fe0 18600060
  //   18601860 6000600 18601860 18600060 1b181b18 c600c60 31103180 36303030 306037f8 33183018 33183318
  //   30c030c0 33183318 33183018 c5986198 21822182 27f22312 23622632 20c220c2 23622632 23622632 21822182
  //   23622632 23622632 44924492 44224422 44924442 44924492 44224422 44924492 44924492 44424442 44924492
  //   44924492 49524852 21e220c2 27f22312 23622632 20c220c2 23622632 23622632 21822182 23622632 23622632
  //   2f7226da 0 0 40024002 5ffa4012 5ffa4012 4ff24812 5ffa4222 48124822 410a4102 48124432 44524252
  //   40824082 0 10081008 800080 2200220 8880888 8500850 1400140 5080508 a140a14 a540a54 8880850 4100220
  //   8880888 11280a28 c700c30 0 0 0 2200ff8 1800ff0 8240424 10601870 0 200020 4000400 4100220 800080
  //   18001800 0 0 8000400 c180c18 1800180 3100180 c300030 c01ff0 c300030 c300c30 3000300 c300c30 c300030
  //   0 18000000 3000c00 0 c00030 0 80011cc 8180c38 c0c0c0c c081800 c180c0c c080c00 c000c00 c181818
  //   c180c18 1800180 38c000c0 c380c70 c080c00 108c11cc 8700870 c18180c c000c00 6580d4c c300c70 10180018
  //   1800180 c180c08 2800640 6280d68 4300660 1800180 18080c00 6000600 180030 300030 0 0 0 c600c60 6180618
  //   c300c00 c600c60 c300c00 1800180 f800c00 6300630 1800180 c000c0 6300760 1800180 18c618c6 c300c30
  //   6300630 6180618 3f00630 6000600 6300030 1900190 c700c30 1c00340 6300528 c300360 1800340 6100300
  //   1000100 800080 400040 38 16881108 11440884 2800200 4800c00 c00060 600030 4c80280 4800280 c601490
  //   14500c88 888044c 888044c 4d00320 4d00320 3000200 3000200 5100c10 5100c10 c381000 c381000 4c00330
  //   4c00330 6100408 6100408 400140 400140 2000240 2000240 1000100 1000100 18800c80 18800c80 c018c c018c
  //   800060 c00030 c00030 2000200 2000200 8000800 8000800 18d00c10 12001000 294c2a38 284c1838 14101208
  //   10e01010 10e01010 10e01010 10081008 10081008 10081008 3a4e0658 3a4e0658 3a4e0658 e0038 e0038 e0038
  //   10e01010 10e01010 10e01010 6800080 506049a0 4080c08 14101248 1080108 800110 800118 e700aa8 126210a2
  //   42003a0 3a00020 80398 400020 18c40c04 28221820 180c0c04 c201410 14100c08 4868280c 4100300 4800380
  //   8200820 11*0 4000200 2000200 1000100 800080 800040 200010 1ffc 3ffe0080 86004a0 8100410 4100410
  //   4100410 400040 400040 2000100 2000100 4000200 4000200 3ffc0008 3ffc0008 200020 200020 1000080
  //   1000080 8080410 8080410 2000200 2000200 1000080 1000080 2200140 2200140 2000100 2000100 2000100
  //   4000200 4000200 2000100 2000100 2000200 2000200 2000100 3ffe 2200140 20801080 10000800 2000 2000
  //   2000 2000200 2000200 2000200 4000200 4000200 4000200 80010 80010 80010 2802082 2802082 2802082
  //   800100 1e00e00 1ff40808 4000220 800080 400040 800100 0 3ffe 7f00010 40004 1000080 800040 8480844
  //   5000480 8040804 800040 200010 800080 3ffe0080 4000200 1000080 200010 4100228 2000100 8*0 8180818
  //   c180c18 c000c00 8180818 c080c00 18080c00 c180c18 c18180c 1800180 c380c70 8180818 108c11cc 8680868
  //   8080000 c18180c c180c18 c000c00 8080c00 1800180 1800180 ff01998 4300660 1800180 11440760 8*0 d5018c0
  //   7e00630 800080 c300c30 6600c30 1e00600 180618 6300630 3200300 6780630 4180228 b740e30 c001c0 600180
  //   1c00360 1cd00248 c000c00 1c00360 3200300 7300618 3800d60 4180228 3800d60 4100e38 38*0 8180818
  //   c180c18 c180c18 c000c00 8300830 c080c00 c000c00 19981998 838101c e180d18 d180d18 c380c70 28300830
  //   108c11cc c180c18 c18180c c180c18 c000c00 c081800 1800180 8001c0 ff01998 4300660 c180c18 180018
  //   318c318c 318c318c 6180618 18d818d8 6180618 818000c 1b061b06 c180618 15*0 6d80c68 6300630 6300630
  //   60006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
  //   图中有一个空白器件，表示少一个器件，请按照字扩展（容量扩展，地址线扩展）的方式利用第一行的存储器完成最终字库，字库文件需要进行简单的分割
  //   contents of rom_6 (hex, n*v repeats v):
  //   280fffe 53fc5048 420fffe 4bfc4950 11001ffe 2007ffc 13f810a0 21242124 45084508 43f838a0 11081108
  //   3e442220 448845fc 48887dfc 20881080 8207efc 57fe7840 11081108 17f830a0 7f241424 20082008 1000100
  //   841080 104817fe 21082108 888f888 104017c0 10441040 4bfe4894 10a010a0 24401820 11083108 48a048a0
  //   44a044a0 547e4444 1df81150 7e7e1444 20002000 49007dc0 14101008 4017fe 840fbc0 200017fc 107ffc
  //   20003ffc 21102f70 48907ff0 104830a0 12041204 28822882 49107bfc 40244004 42043e04 22202210 8203ff8
  //   20a02010 20a02010 49203efe 27fc2048 10001ffe 22201140 11101110 6800880 17fc3040 8200820 1040100
  //   44427ffe 47e44404 27fc1048 111030a0 12203140 3ff82008 1000100 48407c40 20881040 14443444 40844084
  //   11fe1084 14441020 4a884c88 14081090 1441344 13f83208 2040200 fffe0104 52807f4c 10fe1084 104017c0
  //   480848a0 45fe7c00 49fe4400 24200420 25fe0400 257e2494 11180208 108013fe 48447c40 13fe1000 4bfc7c48
  //   11fc1028 17fc3048 11fc1028 8200800 7fe1044 5600300 10400840 20203fe 14500440 2a810a0 10001000 240010
  //   2200200 160213fe 40027ffe 1202fffe 121011f8 4a107df8 7d0221fe 340227fe 40027ffe 220223fe 200fffe
  //   4a024bfe 104037fc 1000100 40100 104017fc 420c4004 27fc1008 784007fc 207cff44 1000fffe 10007ffc
  //   3ffc0090 203ff8 4aa42a90 20881040 fffe0104 20802ffc 12241110 41244104 49fe7c94 11fe1094 4800c80
  //   24fe2444 21fe2094 920fffe 440fffe 1040100 17fe0844 10440940 20082008 27fe2044 7ffc0108 820fffe
  //   4bfc7c48 1ff01110 3ff82108 4a487e48 112411fe 10080840 17fc3444 27fc2444 21082108 20fe3f08 2087ffc
  //   10081ffe 12083208 14041020 fffe0104 40244804 20042040 49fe7d04 1110f0f8 8207ffc 40040804 52487910
  //   12100920 12100920 12081408 14881088 12083208 44427ffe 8907890 1050fe50 48404840 12081208 104037c0
  //   1007ffc 49087dfc 1d0811fc 10201ff0 8001800 401040 3ff82008 2000200 440fffe 10881080 4200400 10101010
  //   11101110 483f48 2007ffc 10881080 11000ff8 92905290 208017fc 120009fc 110811fc 3ffc0090 51127ffe
  //   48887c80 51045100 1ffe1004 18200ff0 10881080 12083208 4403ff8 44444444 110011e0 440fffe 1050fc50
  //   107efe40 49207d38 48407ffc 4a087a08 1df81108 509057fe 10d8f020 10101ff8 6c00100 9201110 48e04ffe
  //   7fc0208 111017fc 120813fc 14d81020 1501248 fe0884 3ff82008 24942790 4807ffc 22203ffc 4fffe 110411fe
  //   3ff80100 1dfc1128 13fc3248 4100400 54444b4c 2407e48 212421fe 4a227bfe 142013fe 5ff84010 51127ffe
  //   fe2223fe 54847c84 55fc1028 17fc0848 11fc2c28 2000200 22003ffe 10101ff0 48407c40 24202710 3c202710
  //   1ff81110 20401040 25fe1e54 102011e0 3ffc0090 48a04910 23c01100 23fe3f04 41044804 1102f70 ffe0804
  //   20a02ffe 10101010 511048a0 1128fd08 ff940918 8200820 4a084bfc 3d0820f8 1007ffc 49027ffe 510848f8
  //   49084508 10401048 11041104 22042200 43b83800 1040100 451028a0 3ef80000 1244327e 8200420 fe4429de
  //   fffc10a0 17fc30a0 ff081108 4bfe7c84 7ffc 1044fc20 8207ffc 17fe1224 17fe0a24 7ffe0804 3ffc1048 3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
  //   contents of rom_7 (hex, n*v repeats v):
  //   5*0 10041004 0 3300110 ffc0608 0 0 2400240 0 300030 10000800 cc00cc 44002200 400040 1000100 1000080
  //   400080 4800240 1200240 1000100 800080 28002f8 500050 8800840 880108 78007c0 f001f0 800080 4100808
  //   1800180 1800180 4100220 10042002 6000c04 18181818 10041004 10041004 4000400 1818 200010 800080
  //   1200120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
  //   contents of rom_8 (hex, n*v repeats v):
  //   0 c000c00 48004800 0 0 1c00140 0 11001100 4000e0 0 0 2400240 5*0 380060 e000300 400080 200 240 240
  //   1000100 f800080 3800280 10101fd0 ff00820 7f80208 7f007e0 7f003f0 ff8 808 180 180 2002 1400220
  //   1ffc1ffc 3c3c1818 c18180c 10041004 3000400 1818 c002e00 1ffc0080 4800480 0 0 c181004 c001200 c001200
  //   5*0 20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
  //   请在下方利用上方输入输出引脚的隧道信号构建电路，ctrl+d复制选择部件
  //   汉字显示验证区
  //   contents of rom_9 (hex, n*v repeats v):
  //   7*0 1100000 3000380 0 0 2400240 0 100008 c000c00 440022 33003300 600038 3000e00 400000 1000200
  //   2400000 2400000 10001f0 800080 20803f8 500070 8200ff0 20807f8 7e007f0 3f007f0 800080 0 0 0 2200140
  //   20020000 18041ffc 18183ffc 10041004 180c0c18 30000c0 18180000 100008 800080 1200120 100008 63001c0
  //   2002100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
  //   contents of rom_10 (hex, n*v repeats v):
  //   0 0 0 1800000 7f00000 8080808 c300000 6600330 10300c18 7ffe0000 3f800e00 2400240 318c0000 4*0 400040
  //   1000100 4000200 100020 9000480 900120 1000100 800080 2800280 500050 9000880 480088 7000780 7000f0
  //   800ff8 1400220 0 0 8080410 8081004 3000300 18181818 10041004 10041004 8000800 0 400020 800080
  //   2400240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
  //   contents of rom_11 (hex, n*v repeats v):
  //   0 0 3000 0 0 80 5*0 240 5*0 c 1800 7*0 1ff0 9*0 80 0 0 7f0 1004 c0 0 400 4*0 3e0 7*0 200 20c 0 60018
  //   30000c00 10*0 21c2 400 430 0 1c0 605e 2002 2002 0 0 3e0 80 80 7*0 80 80 3ffc 16*0 7b0 8*0 3ce6 1ef6
  //   9*0 9*808 11*1008 10*3e0 0 0 10*1008 23*0 4 2000 17*0 2000 c 0 3000 180 17*0 300048 9*0 7f8 2 ff0 9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
endmodule

module \字库测试  (
);

  wire CLK, comparator_1_eq, d_ff_1_q, not_1_out;
  wire [7:0] counter_1_q;
  wire [15:0] adder_1_out, rom_1_data;
  wire [31:0] R2, R2_S, \参考字库_1_d0 , \参考字库_1_d3 , \参考字库_1_d4 , \参考字库_1_d5 , \参考字库_1_d6 , \参考字库_1_d6_2 ,
       \参考字库_1_d7 , \字库电路_1_d0 , \字库电路_1_d3 , \字库电路_1_d4 , \字库电路_1_d5 , \字库电路_1_d6 , \字库电路_1_d6_2 ,
       \字库电路_1_d7 ;

  Counter counter_1 (.Q(counter_1_q), .clk(CLK));  // open: load, D, count, carry, clr
  Clock clock_1 (.out(CLK));
  ROM #(.dataWidth(16)) rom_1 (.addr(counter_1_q), .data(rom_1_data));  // open: sel
  Adder #(.width(16)) adder_1 (.a(rom_1_data), .b(16'h5f60), .out(adder_1_out));  // open: cin, cout
  \字库电路  \u_字库电路_1  (
    .D0(\字库电路_1_d0 ), .D1(R2), .D6(\字库电路_1_d6 ), .D3(\字库电路_1_d3 ), .\区号 (adder_1_out[14:8]),
    .\位号 (adder_1_out[6:0]), .D4(\字库电路_1_d4 ), .D5(\字库电路_1_d5 ), .D6_2(\字库电路_1_d6_2 ), .D7(\字库电路_1_d7 ));
  \参考字库  \u_参考字库_1  (
    .D0(\参考字库_1_d0 ), .D1(R2_S), .D6(\参考字库_1_d6 ), .D3(\参考字库_1_d3 ), .\区号 (adder_1_out[14:8]),
    .\位号 (adder_1_out[6:0]), .D4(\参考字库_1_d4 ), .D5(\参考字库_1_d5 ), .D6_2(\参考字库_1_d6_2 ), .D7(\参考字库_1_d7 ));
  Pull_Resistor #(.pull(1)) pull_resistor_1 (.node(R2));
  DotMatrix #(.inputtype("row"), .matrixcols(16), .matrixrows(16), .dotshape("circle")) dotmatrix_1 (
    .row0(\字库电路_1_d0 [15:0]), .row1(\字库电路_1_d0 [31:16]), .row2(R2[15:0]), .row3(R2[31:16]),
    .row4(\字库电路_1_d6 [15:0]), .row5(\字库电路_1_d6 [31:16]), .row6(\字库电路_1_d3 [15:0]), .row7(\字库电路_1_d3 [31:16]),
    .row8(\字库电路_1_d4 [15:0]), .row9(\字库电路_1_d4 [31:16]), .row10(\字库电路_1_d5 [15:0]),
    .row11(\字库电路_1_d5 [31:16]), .row12(\字库电路_1_d6_2 [15:0]), .row13(\字库电路_1_d6_2 [31:16]),
    .row14(\字库电路_1_d7 [15:0]), .row15(\字库电路_1_d7 [31:16]));
  DotMatrix #(.inputtype("row"), .matrixcols(16), .matrixrows(16), .dotshape("circle")) dotmatrix_2 (
    .row0(\参考字库_1_d0 [15:0]), .row1(\参考字库_1_d0 [31:16]), .row2(R2_S[15:0]), .row3(R2_S[31:16]),
    .row4(\参考字库_1_d6 [15:0]), .row5(\参考字库_1_d6 [31:16]), .row6(\参考字库_1_d3 [15:0]), .row7(\参考字库_1_d3 [31:16]),
    .row8(\参考字库_1_d4 [15:0]), .row9(\参考字库_1_d4 [31:16]), .row10(\参考字库_1_d5 [15:0]),
    .row11(\参考字库_1_d5 [31:16]), .row12(\参考字库_1_d6_2 [15:0]), .row13(\参考字库_1_d6_2 [31:16]),
    .row14(\参考字库_1_d7 [15:0]), .row15(\参考字库_1_d7 [31:16]));
  Comparator #(.width(32)) comparator_1 (.a(R2_S), .b(R2), .eq(comparator_1_eq));  // open: gt, lt
  not not_1 (not_1_out, comparator_1_eq);
  LED led_1 (.in(d_ff_1_q));
  D_Flip_Flop #(.trigger("high")) d_ff_1 (.clk(CLK), .D(not_1_out), .Q(d_ff_1_q));  // open: Qn, preset, en, reset

  // Notes on the sheet:
  //   GB2312
  //   contents of rom_1 (hex, n*v repeats v):
  //   bbaa d6d0 bfc6 bcbc b4f3 d1a7 cac7 b9fa bcd2 bdcc d3fd b2bf d6b1 caf4 b5c4 c8ab b9fa d6d8 b5e3 b4f3
  //   d1a7 a3ac d3c9 d4ad bbaa d6d0 c0ed b9a4 b4f3 d1a7 a1a2 cdac bcc3 d2bd bfc6 b4f3 d1a7 a1a2 cee4 baba
  //   b3c7 cad0 bda8 c9e8 d1a7 d4ba d3da a3b2 a3b0 a3b0 a3b0 c4ea a3b5 d4c2 a3b2 a3b6 c8d5 bacf b2a2 b3c9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
  //   电路功能：字库实现正确性检测，通过对比标准库与待测字库的显示检验功能正确性，ctrl+K驱动电路进行自动仿真
  //   标准库
  //   红灯亮表示有故障
endmodule

// 参考字库
module \参考字库  (
  input  [6:0] \区号 ,
  input  [6:0] \位号 ,
  output [31:0] D0,
  output [31:0] D1,
  output [31:0] D6,
  output [31:0] D3,
  output [31:0] D4,
  output [31:0] D5,
  output [31:0] D6_2,
  output [31:0] D7
);

  wire [6:0] multiplier_1_cout, multiplier_1_out, subtractor_1_out;
  wire [13:0] adder_1_out, bit_extender_1_out, subtractor_2_out;

  ROM #(.addrWidth(14), .dataWidth(32)) rom_1 (.addr(subtractor_2_out), .data(D0));  // open: sel
  ROM #(.addrWidth(14), .dataWidth(32)) rom_2 (.addr(subtractor_2_out), .data(D4));  // open: sel
  Subtractor #(.width(7)) subtractor_1 (.a(\区号 ), .b(7'b0000001), .out(subtractor_1_out));  // open: bin, bout
  Multiplier #(.width(7)) multiplier_1 (
    .a(subtractor_1_out), .b(7'b1011110), .out(multiplier_1_out), .cout(multiplier_1_cout));  // open: cin
  ROM #(.addrWidth(14), .dataWidth(32)) rom_3 (.addr(subtractor_2_out), .data(D1));  // open: sel
  ROM #(.addrWidth(14), .dataWidth(32)) rom_4 (.addr(subtractor_2_out), .data(D5));  // open: sel
  Adder #(.width(14)) adder_1 (
    .a({multiplier_1_cout, multiplier_1_out}), .b(bit_extender_1_out), .out(adder_1_out));  // open: cin, cout
  assign bit_extender_1_out = {{7{1'b0}}, \位号 };  // Bit_Extender bit_extender_1
  ROM #(.addrWidth(14), .dataWidth(32)) rom_5 (.addr(subtractor_2_out), .data(D6));  // open: sel
  ROM #(.addrWidth(14), .dataWidth(32)) rom_6 (.addr(subtractor_2_out), .data(D6_2));  // open: sel
  Subtractor #(.width(14)) subtractor_2 (.a(adder_1_out), .b(14'h1), .out(subtractor_2_out));  // open: bin, bout
  DotMatrix #(.inputtype("row"), .matrixcols(16), .matrixrows(16), .dotshape("circle")) dotmatrix_1 (
    .row0(D0[15:0]), .row1(D0[31:16]), .row2(D1[15:0]), .row3(D1[31:16]), .row4(D6[15:0]), .row5(D6[31:16]),
    .row6(D3[15:0]), .row7(D3[31:16]), .row8(D4[15:0]), .row9(D4[31:16]), .row10(D5[15:0]),
    .row11(D5[31:16]), .row12(D6_2[15:0]), .row13(D6_2[31:16]), .row14(D7[15:0]), .row15(D7[31:16]));
  ROM #(.addrWidth(14), .dataWidth(32)) rom_7 (.addr(subtractor_2_out), .data(D3));  // open: sel
  ROM #(.addrWidth(14), .dataWidth(32)) rom_8 (.addr(subtractor_2_out), .data(D7));  // open: sel

  // Other names for the same wires on the sheet: D2[31:0] = D6; D6_t[31:0] = D6_2

  // Notes on the sheet:
  //   输入引脚区
  //   输入引脚区
  //   contents of rom_1 (hex, n*v repeats v):
  //   8*0 1000000 0 0 2400000 5*0 c0000 18000000 16*0 800000 0 0 0 10040000 7f00000 0 0 80000 800000 0 0 0
  //   c1803e0 0 600000 5*0 200000 0 18200000 180006 c003000 0 0 0 800000 1c00000 1c00000 200000 900000
  //   48003000 0 0 500000 0 40000 1c00000 38300000 800080 800080 3c00000 3c00000 c1803e0 1400080 1c00080 0
  //   0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
  //   contents of rom_2 (hex, n*v repeats v):
  //   0 0 0 180 0 4100410 c30 4400440 2600030 0 fe61c3 2400240 318c 4*0 400040 1000100 4000800 400020
  //   4800900 1200090 1000100 800080 2800280 500050 8800900 880048 7800700 f00070 800080 1400080 1ff8 0
  //   10040808 4100808 4000200 18181818 10041004 10041004 8000fc0 0 800040 800080 2400240 4000200 20022002
  //   40814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
  //   输出引脚区
  //   电路功能：汉字16*16点阵字库文件，修改引脚区的区号位号即可显示不同的汉字，字库数据可以导出供具体实验具体实现时使用
  //   contents of rom_3 (hex, n*v repeats v):
  //   7*0 1100000 3000380 0 0 2400240 0 100008 c000c00 440022 33003300 600038 3000e00 400000 1000200
  //   2400000 2400000 10001f0 800080 20803f8 500070 8200ff0 20807f8 7e007f0 3f007f0 800080 0 0 0 2200140
  //   20020000 18041ffc 18183ffc 10041004 180c0c18 30000c0 18180000 100008 800080 1200120 100008 63001c0
  //   2002100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
  //   contents of rom_4 (hex, n*v repeats v):
  //   0 18002000 30000000 0 0 2200220 0 8800880 c001c0 0 38 2400240 5*0 400040 1000100 1000200 1000080
  //   2400480 2400120 1000100 800080 2800280 500050 8400880 1080088 7c00780 1f000f0 80 4100220 1800000
  //   1800000 20021004 2200410 8040400 18181818 10041004 10041004 4000800 18180000 3b001080 800080 4800480
  //   1ff80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
  //   提示：多路选择器，译码器，到底用哪个，还是两个都用，哪个成本更低？
  //   16*16点阵需要32个字节256位数据才能显示一个汉字，这里利用8个32位ROM存储器位扩展构成一次能访问256位点阵码的字库
  //   contents of rom_5 (hex, n*v repeats v):
  //   5*0 10041004 0 3300110 ffc0608 0 0 2400240 0 300030 10000800 cc00cc 44002200 400040 1000100 1000080
  //   400080 4800240 1200240 1000100 800080 28002f8 500050 8800840 880108 78007c0 f001f0 800080 4100808
  //   1800180 1800180 4100220 10042002 6000c04 18181818 10041004 10041004 4000400 1818 200010 800080
  //   1200120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
  //   contents of rom_6 (hex, n*v repeats v):
  //   0 c000c00 48004800 0 0 1c00140 0 11001100 4000e0 0 0 2400240 5*0 380060 e000300 400080 200 240 240
  //   1000100 f800080 3800280 10101fd0 ff00820 7f80208 7f007e0 7f003f0 ff8 808 180 180 2002 1400220
  //   1ffc1ffc 3c3c1818 c18180c 10041004 3000400 1818 c002e00 1ffc0080 4800480 0 0 c181004 c001200 c001200
  //   5*0 20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
  //   将区号，位号计算成存储器的偏移地址，此部分电路可以复制到实验电路中使用
  //   汉字显示验证区
  //   contents of rom_7 (hex, n*v repeats v):
  //   0 0 0 1800000 7f00000 8080808 c300000 6600330 10300c18 7ffe0000 3f800e00 2400240 318c0000 4*0 400040
  //   1000100 4000200 100020 9000480 900120 1000100 800080 2800280 500050 9000880 480088 7000780 7000f0
  //   800ff8 1400220 0 0 8080410 8081004 3000300 18181818 10041004 10041004 8000800 0 400020 800080
  //   2400240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
  //   contents of rom_8 (hex, n*v repeats v):
  //   0 0 3000 0 0 80 5*0 240 5*0 c 1800 7*0 1ff0 9*0 80 0 0 7f0 1004 c0 0 400 4*0 3e0 7*0 200 20c 0 60018
  //   30000c00 10*0 21c2 400 430 0 1c0 605e 2002 2002 0 0 3e0 80 80 7*0 80 80 3ffc 16*0 7b0 8*0 3ce6 1ef6
  //   9*0 9*808 11*1008 10*3e0 0 0 10*1008 23*0 4 2000 17*0 2000 c 0 3000 180 17*0 300048 9*0 7f8 2 ff0 9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
endmodule

module MIPS_RAM (
  input  [11:0] \字节地址 ,
  input  [31:0] Din,
  input  CLK,
  input  WE,
  input  [1:0] Mode,
  output [31:0] DataOut
);

  wire and_1_out, and_2_out, and_3_out, and_4_out, and_5_out, and_6_out, and_7_out, and_8_out, and_9_out,
       and_10_out, and_11_out, and_12_out, decoder_1_out0, decoder_1_out1, decoder_1_out2, decoder_1_out3,
       decoder_2_out0, decoder_2_out1, decoder_2_out2, decoder_2_out3, Mode_2bytes, Mode_byte, Mode_word,
       not_1_out, not_2_out, or_1_out, or_2_out, or_3_out, or_4_out;
  wire [7:0] Din0, Din1, Din2, Din3, Dout0, Dout1, Dout2, Dout3;
  wire [31:0] _8bit, _16bit, Dout8, Dout16;

  and and_1 (and_1_out, WE, or_1_out);
  or or_1 (or_1_out, and_3_out, and_2_out, Mode_word);
  and and_2 (and_2_out, \字节地址 [1], Mode_2bytes);
  and and_3 (and_3_out, \字节地址 [0], \字节地址 [1], Mode_byte);
  RAM #(.addrWidth(10), .bus("separate")) ram_1 (
    .addr(\字节地址 [11:2]), .din(Din3), .data(Dout3), .str(and_1_out), .clk(CLK));  // open: sel, ld, clr
  and and_4 (and_4_out, \字节地址 [1], ~\字节地址 [0], Mode_byte);  // AND_Gate
  Decoder #(.select(2), .enable("false")) decoder_1 (
    .out0(decoder_1_out0), .out1(decoder_1_out1), .out2(decoder_1_out2), .out3(decoder_1_out3),
    .sel(\字节地址 [1:0]));
  and and_5 (and_5_out, WE, or_2_out);
  or or_2 (or_2_out, and_4_out, and_6_out, Mode_word);
  and and_6 (and_6_out, \字节地址 [1], Mode_2bytes);
  not not_1 (not_1_out, \字节地址 [1]);
  Decoder #(.select(2), .enable("false")) decoder_2 (
    .out0(decoder_2_out0), .out1(decoder_2_out1), .out2(decoder_2_out2), .out3(decoder_2_out3),
    .sel(\字节地址 [1:0]));
  // Probe on DataOut
  RAM #(.addrWidth(10), .bus("separate")) ram_2 (
    .addr(\字节地址 [11:2]), .din(Din2), .data(Dout2), .str(and_5_out), .clk(CLK));  // open: sel, ld, clr
  assign _16bit = \字节地址 [1] ? {Din[15:0], {16{1'b0}}} : 32'bz;  // Controlled_Buffer controlled_buffer_1
  assign _16bit = not_1_out ? {{16{1'b0}}, Din[15:0]} : 32'bz;  // Controlled_Buffer controlled_buffer_2
  assign _8bit = decoder_1_out0 ? {{24{1'b0}}, Din[7:0]} : 32'bz;  // Controlled_Buffer controlled_buffer_3
  assign _8bit = decoder_1_out1 ? {{16{1'b0}}, Din[7:0], {8{1'b0}}} : 32'bz;  // Controlled_Buffer controlled_buffer_4
  assign _8bit = decoder_1_out2 ? {{8{1'b0}}, Din[7:0], {16{1'b0}}} : 32'bz;  // Controlled_Buffer controlled_buffer_5
  assign _8bit = decoder_1_out3 ? {Din[7:0], {24{1'b0}}} : 32'bz;  // Controlled_Buffer controlled_buffer_6
  assign Dout8 = decoder_2_out0 ? {{24{1'b0}}, Dout0} : 32'bz;  // Controlled_Buffer controlled_buffer_7
  assign Dout8 = decoder_2_out1 ? {{24{1'b0}}, Dout1} : 32'bz;  // Controlled_Buffer controlled_buffer_8
  and and_7 (and_7_out, ~\字节地址 [1], \字节地址 [0], Mode_byte);  // AND_Gate
  assign Dout16 = \字节地址 [1] ? {{16{1'b0}}, Dout3, Dout2} : 32'bz;  // Controlled_Buffer controlled_buffer_9
  assign Dout16 = not_2_out ? {{16{1'b0}}, Dout1, Dout0} : 32'bz;  // Controlled_Buffer controlled_buffer_10
  not not_2 (not_2_out, \字节地址 [1]);
  assign Dout8 = decoder_2_out2 ? {{24{1'b0}}, Dout2} : 32'bz;  // Controlled_Buffer controlled_buffer_11
  assign Dout8 = decoder_2_out3 ? {{24{1'b0}}, Dout3} : 32'bz;  // Controlled_Buffer controlled_buffer_12
  and and_8 (and_8_out, WE, or_3_out);
  or or_3 (or_3_out, and_7_out, and_9_out, Mode_word);
  and and_9 (and_9_out, ~\字节地址 [1], Mode_2bytes);  // AND_Gate
  RAM #(.addrWidth(10), .bus("separate")) ram_3 (
    .addr(\字节地址 [11:2]), .din(Din1), .data(Dout1), .str(and_8_out), .clk(CLK));  // open: sel, ld, clr
  and and_10 (and_10_out, ~\字节地址 [1], ~\字节地址 [0], Mode_byte);  // AND_Gate
  nor nor_1 (Mode_word, Mode[0], Mode[1]);
  and and_11 (and_11_out, WE, or_4_out);
  or or_4 (or_4_out, and_10_out, and_12_out, Mode_word);
  and and_12 (and_12_out, ~\字节地址 [1], Mode_2bytes);  // AND_Gate
  Multiplexer #(.select(2), .width(32), .enable("false")) multiplexer_1 (
    .in0(Din), .in1(_8bit), .in2(_16bit), .out({Din3, Din2, Din1, Din0}), .sel(Mode));  // open: in3
  Multiplexer #(.select(2), .width(32), .enable("false")) multiplexer_2 (
    .in0({Dout3, Dout2, Dout1, Dout0}), .in1(Dout8), .in2(Dout16), .out(DataOut), .sel(Mode));  // open: in3
  RAM #(.addrWidth(10), .bus("separate")) ram_4 (
    .addr(\字节地址 [11:2]), .din(Din0), .data(Dout0), .str(and_11_out), .clk(CLK));  // open: sel, ld, clr
  and and_13 (Mode_byte, ~Mode[1], Mode[0]);  // AND_Gate
  and and_14 (Mode_2bytes, Mode[1], ~Mode[0]);  // AND_Gate

  // Other names for the same wires on the sheet: _8bit_high[31:24] = Din[7:0]; _8bit_high2[23:16] = Din[7:0];
  //   _8bit_low[7:0] = Din[7:0]; _8bit_low2[15:8] = Din[7:0]; _16bit_high[31:16] = Din[15:0];
  //   _16bit_low[15:0] = Din[15:0]; _32bit[31:0] = Din; Dout[31:0] = DataOut; Dout8_high[7:0] = Dout3;
  //   Dout16_high[15:0] = {Dout3, Dout2}; Dout32[31:0] = {Dout3, Dout2, Dout1, Dout0}; Dout8_high2[7:0] = Dout2;
  //   Dout8_low[7:0] = Dout0; Dout16_low[15:0] = {Dout1, Dout0}; Dout8_low2[7:0] = Dout1

  // Notes on the sheet:
  //   输入引脚区
  //   请勿增改引脚，请勿修改子电路封装
  //   电路功能：利用下图中给定的RAM器件实现既既可以按照字节，也可以按照半字，也可以按照32位字访问的MIPS存储器
  //   请在下方利用上方输入输出引脚的隧道信号构建电路，ctrl+d复制选择部件
  //   输出引脚区
endmodule

module \MIPS_RAM测试  (
);

  wire clock_1_out, comparator_1_eq, comparator_2_eq, EN, rom_3_data;
  wire [1:0] rom_4_data, rom_5_data;
  wire [7:0] counter_1_q;
  wire [11:0] rom_1_data;
  wire [15:0] multiplexer_1_out, multiplexer_1_out_2;
  wire [31:0] adder_1_out, mips_ram_1_dataout, rom_2_data, \校验和_q ;

  Clock clock_1 (.out(clock_1_out));
  // Probe on counter_1_q
  Counter counter_1 (.count(EN), .Q(counter_1_q), .clk(clock_1_out));  // open: load, D, carry, clr
  ROM #(.dataWidth(12)) rom_1 (.addr(counter_1_q), .data(rom_1_data));  // open: sel
  ROM #(.dataWidth(32)) rom_2 (.addr(counter_1_q), .data(rom_2_data));  // open: sel
  ROM #(.dataWidth(1)) rom_3 (.addr(counter_1_q), .data(rom_3_data));  // open: sel
  ROM #(.dataWidth(2)) rom_4 (.addr(counter_1_q), .data(rom_4_data));  // open: sel
  ROM #(.dataWidth(2)) rom_5 (.addr(counter_1_q), .data(rom_5_data));  // open: sel
  // Probe on rom_1_data
  // Probe on rom_2_data
  // Probe on rom_4_data
  Comparator #(.width(2)) comparator_1 (.a(rom_5_data), .b(2'b11), .eq(comparator_1_eq));  // open: gt, lt
  MIPS_RAM mips_ram_1 (
    .\字节地址 (rom_1_data), .Din(rom_2_data), .DataOut(mips_ram_1_dataout), .CLK(clock_1_out), .WE(rom_3_data),
    .Mode(rom_4_data));
  // Probe on mips_ram_1_dataout
  _7_Segment_Display u_7_segment_display_1 (
    .g(multiplexer_1_out[15]), .f(multiplexer_1_out[14]), .a(multiplexer_1_out[13]),
    .b(multiplexer_1_out[12]), .e(multiplexer_1_out_2[15]), .d(multiplexer_1_out_2[14]),
    .c(multiplexer_1_out_2[13]), .dp(multiplexer_1_out_2[12]));
  _7_Segment_Display u_7_segment_display_2 (
    .g(multiplexer_1_out[11]), .f(multiplexer_1_out[10]), .a(multiplexer_1_out[9]), .b(multiplexer_1_out[8]),
    .e(multiplexer_1_out_2[11]), .d(multiplexer_1_out_2[10]), .c(multiplexer_1_out_2[9]),
    .dp(multiplexer_1_out_2[8]));
  Adder #(.width(32)) adder_1 (.a(\校验和_q ), .b(mips_ram_1_dataout), .out(adder_1_out));  // open: cin, cout
  _7_Segment_Display u_7_segment_display_3 (
    .g(multiplexer_1_out[3]), .f(multiplexer_1_out[2]), .a(multiplexer_1_out[1]), .b(multiplexer_1_out[0]),
    .e(multiplexer_1_out_2[3]), .d(multiplexer_1_out_2[2]), .c(multiplexer_1_out_2[1]),
    .dp(multiplexer_1_out_2[0]));
  _7_Segment_Display u_7_segment_display_4 (
    .g(multiplexer_1_out[7]), .f(multiplexer_1_out[6]), .a(multiplexer_1_out[5]), .b(multiplexer_1_out[4]),
    .e(multiplexer_1_out_2[7]), .d(multiplexer_1_out_2[6]), .c(multiplexer_1_out_2[5]),
    .dp(multiplexer_1_out_2[4]));
  not not_1 (EN, comparator_1_eq);
  Register #(.width(32)) \u_校验和  (.D(adder_1_out), .en(EN), .Q(\校验和_q ), .clk(clock_1_out));  // open: clr
  Multiplexer #(.width(32), .disabled(0)) multiplexer_1 (
    .in0(32'h8a8cef44), .in1(32'h8a66ffee), .out({multiplexer_1_out_2, multiplexer_1_out}),
    .sel(comparator_2_eq), .en(comparator_1_eq));
  Comparator #(.width(32)) comparator_2 (.a(\校验和_q ), .b(32'he1f5edf0), .eq(comparator_2_eq));  // open: gt, lt

  // Notes on the sheet:
  //   Trace存储器
  //   contents of rom_1 (hex, n*v repeats v):
  //   0 4 8 c 10 14 18 1c 20 24 28 2c 30 34 38 3c 2 6 a e 31 35 39 3d 13 17 1b 1f 12 16 1a 1e 11 15 19 1d
  //   10 14 18 1c 0 4 8 c 10 14 18 1c 20 24 28 2c 30 34 38 3c 0 2 4 6 8 a c e 10 12 14 16 18 1a 1c 1e 20
  //   22 24 26 28 2a 2c 2e 30 32 34 36 38 3a 3c 3e 0 1 2 3 4 5 6 7 8 9 a b c d e f 10 11 12 13 14 15 16 17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
  //   contents of rom_2 (hex, n*v repeats v):
  //   203 607 a0b e0f 4*0 20212223 24252627 28292a2b 2c2d2e2f 30310000 34350000 38390000 3c3d0000 1 405
  //   809 c0d 3233 3637 3a3b 3e3f 10 14 18 1c 11 15 19 1d 12 16 1a 1e 13 17 1b 1f
  //   contents of rom_3 (hex, n*v repeats v):
  //   40*1
  //   contents of rom_4 (hex, n*v repeats v):
  //   16*0 8*2 16*1 16*0 32*2 65*1
  //   contents of rom_5 (hex, n*v repeats v):
  //   16*0 8*2 16*1 16*0 32*2 64*1 3
  //   电路功能：测试MIPS RAM存储器， ctrl+k启动时钟后，会自动对完成的MIPS RAM存储器进行读写测试，并将最终写入的数据逐一读出进行校验和计算
  //   电路状态稳定后测试正确显示PASS，错误显示FAIL
endmodule

module MIPS_Regfile (
  input  [4:0] R1_num,
  input  [4:0] R2_num,
  input  [31:0] Din,
  input  [4:0] Write_Reg_num,
  input  Write_Enable,
  input  Clock,
  output [31:0] Reg1Out,
  output [31:0] Reg2Out
);

  wire and_1_out, and_2_out, and_3_out;
  wire [31:0] demultiplexer_1_out1, demultiplexer_1_out2, demultiplexer_1_out3, register_1_q, register_2_q,
       register_3_q, register_4_q;

  Demultiplexer #(.select(2), .width(32), .enable("false")) demultiplexer_1 (
    .out1(demultiplexer_1_out1), .out2(demultiplexer_1_out2), .out3(demultiplexer_1_out3), .in(Din),
    .sel(Write_Reg_num[1:0]));  // open: out0
  and and_1 (and_1_out, Write_Enable, ~Write_Reg_num[1], Write_Reg_num[0]);  // AND_Gate
  and and_2 (and_2_out, Write_Enable, Write_Reg_num[1], ~Write_Reg_num[0]);  // AND_Gate
  and and_3 (and_3_out, Write_Enable, Write_Reg_num[0], Write_Reg_num[1]);
  Register #(.width(32)) register_1 (.D({32{1'b0}}), .en(Write_Enable), .Q(register_1_q), .clk(Clock));  // open: clr
  Register #(.width(32)) register_2 (
    .D(demultiplexer_1_out1), .en(and_1_out), .Q(register_2_q), .clk(Clock));  // open: clr
  Register #(.width(32)) register_3 (
    .D(demultiplexer_1_out2), .en(and_2_out), .Q(register_3_q), .clk(Clock));  // open: clr
  Register #(.width(32)) register_4 (
    .D(demultiplexer_1_out3), .en(and_3_out), .Q(register_4_q), .clk(Clock));  // open: clr
  Multiplexer #(.select(2), .width(32), .enable("false")) multiplexer_1 (
    .in0(register_1_q), .in1(register_2_q), .in2(register_3_q), .in3(register_4_q), .out(Reg1Out),
    .sel(R1_num[1:0]));
  Multiplexer #(.select(2), .width(32), .enable("false")) multiplexer_2 (
    .in0(register_1_q), .in1(register_2_q), .in2(register_3_q), .in3(register_4_q), .out(Reg2Out),
    .sel(R2_num[1:0]));

  // Other names for the same wires on the sheet: CLK = Clock; R1_num_t[1:0] = R1_num[1:0];
  //   R2_num_t[1:0] = R2_num[1:0]; RD1[31:0] = Reg1Out; RD2[31:0] = Reg2Out; WE = Write_Enable;
  //   W_num[1:0] = Write_Reg_num[1:0]

  // Notes on the sheet:
  //   输入引脚
  //   电路功能：实现MIPS寄存器组，为简化工作量，寄存器编号高3位不要，最终电路中只需要实现0-3号寄存器，注意0号寄存器恒零
  //   输出引脚
  //   请仔细测试电路，核对功能无误后提交教师进行自动检测评分
endmodule

module \MIPS_Regfile测试  (
);

  wire and_1_out, CLK, comparator_1_eq, comparator_2_eq, comparator_3_eq, comparator_4_eq, Equal, NEQ, nHalt,
       not_1_out, priority_encoder_1_gs, priority_encoder_2_gs, R1_NEQ, R2_NEQ;
  wire [3:0] _1, _2, _3;
  wire [9:0] counter_1_q, counter_2_q;
  wire [15:0] ErrorTrace, otherinput;
  wire [31:0] R1_Ref, R2_Ref, Reg1, Reg2, \regfile评分逻辑_1_total , \regfile评分逻辑_1_正确条数 , WriteData;

  Clock clock_1 (.out(CLK));
  Counter #(.width(10), .max('h3ff)) counter_1 (
    .count(nHalt), .Q(counter_1_q), .clk(CLK));  // open: load, D, carry, clr
  LED #(.active("false")) \u_测试完成  (.in(nHalt));
  Counter #(.width(10), .max('h3ff)) counter_2 (
    .count(NEQ), .Q(counter_2_q), .clk(CLK), .clr(not_1_out));  // open: load, D, carry
  not not_1 (not_1_out, nHalt);
  Comparator #(.width(32)) comparator_1 (.a(R1_Ref), .b(Reg1), .eq(comparator_1_eq));  // open: gt, lt
  Comparator #(.width(32)) comparator_2 (.a(R2_Ref), .b(Reg2), .eq(comparator_2_eq));  // open: gt, lt
  Multiplexer #(.width(8), .enable("false")) multiplexer_1 (
    .in0({8{1'b1}}), .in1({3'b000, otherinput[9:5]}), .out(ErrorTrace[7:0]), .sel(R2_NEQ));
  Multiplexer #(.width(8), .enable("false")) multiplexer_2 (
    .in0({8{1'b1}}), .in1({3'b000, otherinput[4:0]}), .out(ErrorTrace[15:8]), .sel(R1_NEQ));
  ROM #(.addrWidth(10), .dataWidth(32)) rom_1 (.addr(counter_1_q), .data(WriteData));  // open: sel
  ROM #(.addrWidth(10), .dataWidth(16)) rom_2 (.addr(counter_1_q), .data(otherinput));  // open: sel
  ROM #(.addrWidth(10), .dataWidth(32)) rom_3 (.addr(counter_1_q), .data(R1_Ref));  // open: sel
  and and_1 (and_1_out, nHalt, NEQ);
  Priority_Encoder #(.select(1)) priority_encoder_1 (
    .in0(comparator_1_eq), .in1(comparator_1_eq), .gs(priority_encoder_1_gs));  // open: out, en_out, en_in
  Priority_Encoder #(.select(1)) priority_encoder_2 (
    .in0(comparator_2_eq), .in1(comparator_2_eq), .gs(priority_encoder_2_gs));  // open: out, en_out, en_in
  RAM #(.addrWidth(10), .dataWidth(16), .bus("separate")) ram_1 (
    .addr(counter_2_q), .din(ErrorTrace), .str(and_1_out), .clk(CLK));  // open: data, sel, ld, clr
  not not_2 (R1_NEQ, priority_encoder_1_gs);
  and and_2 (Equal, priority_encoder_1_gs, priority_encoder_2_gs);
  not not_3 (NEQ, Equal);
  not not_4 (R2_NEQ, priority_encoder_2_gs);
  Hex_Digit_Display hex_digit_display_1 (.value(_3));  // open: dp
  MIPS_Regfile mips_regfile_1 (
    .R1_num(otherinput[4:0]), .R2_num(otherinput[9:5]), .Write_Reg_num(otherinput[14:10]), .Din(WriteData),
    .Write_Enable(otherinput[15]), .Clock(CLK), .Reg1Out(Reg1), .Reg2Out(Reg2));
  // Probe on otherinput[4:0]
  // Probe on otherinput[9:5]
  ROM #(.addrWidth(10), .dataWidth(32)) rom_4 (.addr(counter_1_q), .data(R2_Ref));  // open: sel
  Hex_Digit_Display hex_digit_display_2 (.value(_2));  // open: dp
  Hex_Digit_Display hex_digit_display_3 (.value(_1));  // open: dp
  Comparator #(.width(32)) comparator_3 (.a(WriteData), .b({32{1'b0}}), .eq(comparator_3_eq));  // open: gt, lt
  Comparator #(.width(16)) comparator_4 (.a(otherinput), .b({16{1'b0}}), .eq(comparator_4_eq));  // open: gt, lt
  \Regfile评分逻辑  \regfile评分逻辑_1  (
    .EQ(Equal), .EN(nHalt), .CLK(CLK), .\正确条数 (\regfile评分逻辑_1_正确条数 ), .High(_3), .Low(_1), .Mid(_2),
    .Total(\regfile评分逻辑_1_total ));  // open: Right
  // Probe on \regfile评分逻辑_1_total 
  nand nand_1 (nHalt, comparator_3_eq, comparator_4_eq);
  // Probe on \regfile评分逻辑_1_正确条数 

  // Other names for the same wires on the sheet: r1_num[4:0] = otherinput[4:0]; r2_num[4:0] = otherinput[9:5];
  //   w_num[4:0] = otherinput[14:10]

  // Notes on the sheet:
  //   测试逻辑伪代码：for(i=0;i<N;i++)   
  //   {
  //   }
  //   Write Trace
  //   WE W# R2# R1# Trace
  //   R1 Trace
  //   写寄存器，使reg[i]=i+1; 
  //   容错处理
  //   contents of rom_1 (hex, n*v repeats v):
  //   1 41b8 1bfe 2 44a8 1ca7 3 5f7a 2f2a 4 3d39 6009
  //   contents of rom_2 (hex, n*v repeats v):
  //   8041 c20 462 8441 820 62 8841 20 c62 8c41 820 462
  //   contents of rom_3 (hex, n*v repeats v):
  //   6*0 2 0 3 2 0 3
  //   错误记录R1#R2#
  //   R2 Trace
  //   每次读两个寄存器遍历所有寄存器与标准值比较，如发生异常记录错误寄存器编号；
  //   如果修改过引脚封装外观，可能需要手工连线调整
  //   contents of rom_4 (hex, n*v repeats v):
  //   4*0 2 0 0 2 0 3 2 4
  //   华中科技大学：计算机组成课程组
  //   成绩
  //   trace全零停止
endmodule

module \Cache_直接相联  (
  input  [31:0] BlockDataIn,
  input  [15:0] Addr,
  input  BlkDataReady,
  input  CLK,
  output Miss,
  output [7:0] DataOut
);


  // Other names for the same wires on the sheet: Blk[31:0] = BlockDataIn; BlkReady = BlkDataReady; 字节地址[15:0] = Addr

  // Notes on the sheet:
  //   输入引脚区
  //   请勿增改引脚，请勿修改子电路封装
  //   电路功能：利用上面给定的隧道构建8行的Cache，cache映射方式自选
  //   请在下方利用上方输入输出引脚的隧道信号构建电路，ctrl+d复制选择部件
  //   输出引脚区
endmodule

module \Cache_全相联  (
  input  [31:0] BlockDataIn,
  input  [15:0] Addr,
  input  BlkDataReady,
  input  CLK,
  output Miss,
  output [7:0] DataOut
);

  wire comparator_1_eq, comparator_2_eq, comparator_3_eq, comparator_4_eq, comparator_5_eq, comparator_6_eq,
       comparator_7_eq, comparator_8_eq, CWriteL0, CWriteL1, CWriteL2, CWriteL3, CWriteL4, CWriteL5,
       CWriteL6, CWriteL7, Hit, L0, L1, L2, L3, L4, L5, L6, L7, not_1_out, not_2_out, not_3_out, not_4_out,
       not_5_out, not_6_out, not_7_out, not_8_out, not_10_out, priority_encoder_1_gs, V0, V1, V2, V3, V4, V5,
       V6, V7, WriteL0, WriteL1, WriteL2, WriteL3, WriteL4, WriteL5, WriteL6, WriteL7;
  wire [2:0] controlled_buffer_1_out, \max3_归并比较_1_max_num , \max3_归并比较_2_max_num , \max3_归并比较_3_max_num ,
       \max3_归并比较_4_max_num , \max3_归并比较_5_max_num , \max3_归并比较_6_max_num , \max3_归并比较_7_max_num ,
       priority_encoder_1_out;
  wire [13:0] Tag0, Tag1, Tag2, Tag3, Tag4, Tag5, Tag6, Tag7;
  wire [15:0] C0, C1, C2, C3, C4, C5, C6, C7, \max3_归并比较_1_max , \max3_归并比较_2_max , \max3_归并比较_3_max ,
       \max3_归并比较_4_max , \max3_归并比较_5_max , \max3_归并比较_6_max ;
  wire [31:0] controlled_buffer_3_out, register_1_q, register_2_q, register_3_q, register_4_q, register_5_q,
       register_6_q, register_7_q, register_8_q;

  Comparator #(.width(14)) comparator_1 (.a(Addr[15:2]), .b(Tag0), .eq(comparator_1_eq));  // open: gt, lt
  Comparator #(.width(14)) comparator_2 (.a(Addr[15:2]), .b(Tag1), .eq(comparator_2_eq));  // open: gt, lt
  Comparator #(.width(14)) comparator_3 (.a(Addr[15:2]), .b(Tag2), .eq(comparator_3_eq));  // open: gt, lt
  Comparator #(.width(14)) comparator_4 (.a(Addr[15:2]), .b(Tag3), .eq(comparator_4_eq));  // open: gt, lt
  Comparator #(.width(14)) comparator_5 (.a(Addr[15:2]), .b(Tag4), .eq(comparator_5_eq));  // open: gt, lt
  Comparator #(.width(14)) comparator_6 (.a(Addr[15:2]), .b(Tag5), .eq(comparator_6_eq));  // open: gt, lt
  Comparator #(.width(14)) comparator_7 (.a(Addr[15:2]), .b(Tag6), .eq(comparator_7_eq));  // open: gt, lt
  Comparator #(.width(14)) comparator_8 (.a(Addr[15:2]), .b(Tag7), .eq(comparator_8_eq));  // open: gt, lt
  and and_1 (L0, V0, comparator_1_eq);
  and and_2 (L1, V1, comparator_2_eq);
  and and_3 (L2, V2, comparator_3_eq);
  and and_4 (L3, V3, comparator_4_eq);
  and and_5 (L4, V4, comparator_5_eq);
  and and_6 (L5, V5, comparator_6_eq);
  and and_7 (L6, V6, comparator_7_eq);
  and and_8 (L7, V7, comparator_8_eq);
  not not_1 (not_1_out, V7);
  not not_2 (not_2_out, V6);
  not not_3 (not_3_out, V6);
  not not_4 (not_4_out, V4);
  not not_5 (not_5_out, V3);
  not not_6 (not_6_out, V2);
  not not_7 (not_7_out, V1);
  not not_8 (not_8_out, V0);
  Priority_Encoder priority_encoder_1 (
    .in0(not_1_out), .in1(not_2_out), .in2(not_3_out), .in3(not_4_out), .in4(not_5_out), .in5(not_6_out),
    .in6(not_7_out), .in7(not_8_out), .out(priority_encoder_1_out), .gs(priority_encoder_1_gs));  // open: en_in, en_out
  \Max3_归并比较  \max3_归并比较_1  (
    .Y(C1), .X(C0), .Y_num(3'b110), .X_num(3'b111), .MAX(\max3_归并比较_1_max ), .Max_num(\max3_归并比较_1_max_num ));
  \Max3_归并比较  \max3_归并比较_2  (
    .Y(C3), .X(C2), .Y_num(3'b100), .X_num(3'b101), .MAX(\max3_归并比较_2_max ), .Max_num(\max3_归并比较_2_max_num ));
  \Max3_归并比较  \max3_归并比较_3  (
    .Y(C5), .X(C4), .Y_num(3'b010), .X_num(3'b011), .MAX(\max3_归并比较_3_max ), .Max_num(\max3_归并比较_3_max_num ));
  \Max3_归并比较  \max3_归并比较_4  (
    .Y(C7), .X(C6), .Y_num(3'b000), .X_num(3'b001), .MAX(\max3_归并比较_4_max ), .Max_num(\max3_归并比较_4_max_num ));
  or or_1 (Hit, L0, L1, L2, L3, L4, L5, L6, L7);
  \Max3_归并比较  \max3_归并比较_5  (
    .Y(\max3_归并比较_2_max ), .X(\max3_归并比较_1_max ), .Y_num(\max3_归并比较_2_max_num ),
    .X_num(\max3_归并比较_1_max_num ), .MAX(\max3_归并比较_5_max ), .Max_num(\max3_归并比较_5_max_num ));
  \Max3_归并比较  \max3_归并比较_6  (
    .Y(\max3_归并比较_4_max ), .X(\max3_归并比较_3_max ), .Y_num(\max3_归并比较_4_max_num ),
    .X_num(\max3_归并比较_3_max_num ), .MAX(\max3_归并比较_6_max ), .Max_num(\max3_归并比较_6_max_num ));
  not not_9 (Miss, Hit);
  \Max3_归并比较  \max3_归并比较_7  (
    .Y(\max3_归并比较_6_max ), .X(\max3_归并比较_5_max ), .Y_num(\max3_归并比较_6_max_num ),
    .X_num(\max3_归并比较_5_max_num ), .Max_num(\max3_归并比较_7_max_num ));  // open: MAX
  Register #(.width(1)) VALID (.D(1'b1), .en(WriteL0), .Q(V0), .clk(CLK));  // open: clr
  Register #(.width(1)) VALID_2 (.D(1'b1), .en(WriteL1), .Q(V1), .clk(CLK));  // open: clr
  Register #(.width(1)) VALID_3 (.D(1'b1), .en(WriteL2), .Q(V2), .clk(CLK));  // open: clr
  Register #(.width(1)) VALID_4 (.D(1'b1), .en(WriteL3), .Q(V3), .clk(CLK));  // open: clr
  Register #(.width(1)) VALID_5 (.D(1'b1), .en(WriteL4), .Q(V4), .clk(CLK));  // open: clr
  Register #(.width(1)) VALID_6 (.D(1'b1), .en(WriteL5), .Q(V5), .clk(CLK));  // open: clr
  Register #(.width(1)) VALID_7 (.D(1'b1), .en(WriteL6), .Q(V6), .clk(CLK));  // open: clr
  Register #(.width(1)) VALID_8 (.D(1'b1), .en(WriteL7), .Q(V7), .clk(CLK));  // open: clr
  assign controlled_buffer_1_out = priority_encoder_1_gs ? priority_encoder_1_out : 3'bz;  // Controlled_Buffer controlled_buffer_1
  not not_10 (not_10_out, priority_encoder_1_gs);
  assign controlled_buffer_1_out = not_10_out ? \max3_归并比较_7_max_num  : 3'bz;  // Controlled_Buffer controlled_buffer_2
  Decoder #(.select(3), .disabled(0), .enable("false")) decoder_1 (
    .out0(CWriteL7), .out1(CWriteL6), .out2(CWriteL5), .out3(CWriteL4), .out4(CWriteL3), .out5(CWriteL2),
    .out6(CWriteL1), .out7(CWriteL0), .sel(controlled_buffer_1_out));
  Register #(.width(14)) TAG (.D(Addr[15:2]), .en(WriteL0), .Q(Tag0), .clk(CLK));  // open: clr
  Register #(.width(14)) TAG_2 (.D(Addr[15:2]), .en(WriteL1), .Q(Tag1), .clk(CLK));  // open: clr
  Register #(.width(14)) TAG_3 (.D(Addr[15:2]), .en(WriteL2), .Q(Tag2), .clk(CLK));  // open: clr
  Register #(.width(14)) TAG_4 (.D(Addr[15:2]), .en(WriteL3), .Q(Tag3), .clk(CLK));  // open: clr
  Register #(.width(14)) TAG_5 (.D(Addr[15:2]), .en(WriteL4), .Q(Tag4), .clk(CLK));  // open: clr
  Register #(.width(14)) TAG_6 (.D(Addr[15:2]), .en(WriteL5), .Q(Tag5), .clk(CLK));  // open: clr
  Register #(.width(14)) TAG_7 (.D(Addr[15:2]), .en(WriteL6), .Q(Tag6), .clk(CLK));  // open: clr
  Register #(.width(14)) TAG_8 (.D(Addr[15:2]), .en(WriteL7), .Q(Tag7), .clk(CLK));  // open: clr
  Counter #(.width(16), .max('hffff)) \u_淘汰计数  (.count(1'b1), .Q(C0), .clk(CLK), .clr(L0));  // open: load, D, carry
  Counter #(.width(16), .max('hffff)) \u_淘汰计数_2  (.count(1'b1), .Q(C1), .clk(CLK), .clr(L1));  // open: load, D, carry
  Counter #(.width(16), .max('hffff)) \u_淘汰计数_3  (.count(1'b1), .Q(C2), .clk(CLK), .clr(L2));  // open: load, D, carry
  Counter #(.width(16), .max('hffff)) \u_淘汰计数_4  (.count(1'b1), .Q(C3), .clk(CLK), .clr(L3));  // open: load, D, carry
  Counter #(.width(16), .max('hffff)) \u_淘汰计数_5  (.count(1'b1), .Q(C4), .clk(CLK), .clr(L4));  // open: load, D, carry
  Counter #(.width(16), .max('hffff)) \u_淘汰计数_6  (.count(1'b1), .Q(C5), .clk(CLK), .clr(L5));  // open: load, D, carry
  Counter #(.width(16), .max('hffff)) \u_淘汰计数_7  (.count(1'b1), .Q(C6), .clk(CLK), .clr(L6));  // open: load, D, carry
  Counter #(.width(16), .max('hffff)) \u_淘汰计数_8  (.count(1'b1), .Q(C7), .clk(CLK), .clr(L7));  // open: load, D, carry
  Register #(.width(32)) register_1 (.D(BlockDataIn), .en(WriteL0), .Q(register_1_q), .clk(CLK));  // open: clr
  Register #(.width(32)) register_2 (.D(BlockDataIn), .en(WriteL1), .Q(register_2_q), .clk(CLK));  // open: clr
  Register #(.width(32)) register_3 (.D(BlockDataIn), .en(WriteL2), .Q(register_3_q), .clk(CLK));  // open: clr
  Register #(.width(32)) register_4 (.D(BlockDataIn), .en(WriteL3), .Q(register_4_q), .clk(CLK));  // open: clr
  Register #(.width(32)) register_5 (.D(BlockDataIn), .en(WriteL4), .Q(register_5_q), .clk(CLK));  // open: clr
  Register #(.width(32)) register_6 (.D(BlockDataIn), .en(WriteL5), .Q(register_6_q), .clk(CLK));  // open: clr
  Register #(.width(32)) register_7 (.D(BlockDataIn), .en(WriteL6), .Q(register_7_q), .clk(CLK));  // open: clr
  Register #(.width(32)) register_8 (.D(BlockDataIn), .en(WriteL7), .Q(register_8_q), .clk(CLK));  // open: clr
  and and_9 (WriteL7, BlkDataReady, CWriteL7);
  and and_10 (WriteL6, BlkDataReady, CWriteL6);
  and and_11 (WriteL5, BlkDataReady, CWriteL5);
  and and_12 (WriteL4, BlkDataReady, CWriteL4);
  and and_13 (WriteL3, BlkDataReady, CWriteL3);
  and and_14 (WriteL2, BlkDataReady, CWriteL2);
  and and_15 (WriteL1, BlkDataReady, CWriteL1);
  and and_16 (WriteL0, BlkDataReady, CWriteL0);
  assign controlled_buffer_3_out = L0 ? register_1_q : 32'bz;  // Controlled_Buffer controlled_buffer_3
  assign controlled_buffer_3_out = L1 ? register_2_q : 32'bz;  // Controlled_Buffer controlled_buffer_4
  assign controlled_buffer_3_out = L2 ? register_3_q : 32'bz;  // Controlled_Buffer controlled_buffer_5
  assign controlled_buffer_3_out = L3 ? register_4_q : 32'bz;  // Controlled_Buffer controlled_buffer_6
  assign controlled_buffer_3_out = L4 ? register_5_q : 32'bz;  // Controlled_Buffer controlled_buffer_7
  assign controlled_buffer_3_out = L5 ? register_6_q : 32'bz;  // Controlled_Buffer controlled_buffer_8
  assign controlled_buffer_3_out = L6 ? register_7_q : 32'bz;  // Controlled_Buffer controlled_buffer_9
  assign controlled_buffer_3_out = L7 ? register_8_q : 32'bz;  // Controlled_Buffer controlled_buffer_10
  Multiplexer #(.select(2), .width(8)) multiplexer_1 (
    .in0(controlled_buffer_3_out[7:0]), .in1(controlled_buffer_3_out[15:8]),
    .in2(controlled_buffer_3_out[23:16]), .in3(controlled_buffer_3_out[31:24]), .out(DataOut),
    .sel(Addr[1:0]), .en(Hit));

  // Other names for the same wires on the sheet: Blk[31:0] = BlockDataIn; BlkReady = BlkDataReady;
  //   OFFSET[1:0] = Addr[1:0]; 字节地址[15:0] = Addr; Tag[13:0] = Addr[15:2]

  // Notes on the sheet:
  //   输入引脚区
  //   请勿增改引脚，请勿修改子电路封装
  //   电路功能：利用上面给定的隧道构建8行的Cache，cache映射方式自选
  //   请在下方利用上方输入输出引脚的隧道信号构建电路，ctrl+d复制选择部件
  //   输出引脚区
endmodule

module \Cache_2路组相联  (
  input  [31:0] BlockDataIn,
  input  [15:0] Addr,
  input  BlkDataReady,
  input  CLK,
  output Miss,
  output [7:0] DataOut
);


  // Other names for the same wires on the sheet: Blk[31:0] = BlockDataIn; BlkReady = BlkDataReady; 字节地址[15:0] = Addr

  // Notes on the sheet:
  //   输入引脚区
  //   请勿增改引脚，请勿修改子电路封装
  //   电路功能：利用上面给定的隧道构建8行的Cache，cache映射方式自选
  //   请在下方利用上方输入输出引脚的隧道信号构建电路，ctrl+d复制选择部件
  //   输出引脚区
endmodule

module \Cache_4路组相联  (
  input  [31:0] BlockDataIn,
  input  [15:0] Addr,
  input  BlkDataReady,
  input  CLK,
  output Miss,
  output [7:0] DataOut
);

  wire comparator_1_eq, comparator_2_eq, comparator_3_eq, comparator_4_eq, controlled_buffer_9_out,
       controlled_buffer_10_out, controlled_buffer_11_out, controlled_buffer_12_out, CWriteL0, CWriteL1,
       CWriteL2, CWriteL3, CWriteL4, CWriteL5, CWriteL6, CWriteL7, Del0, Del1, Del2, Del3, Hit, k0, k1, k2,
       k3, L0, L1, L2, L3, L4, L5, L6, L7, not_1_out, not_2_out, not_3_out, not_4_out, not_5_out, not_6_out,
       not_7_out, not_8_out, not_9_out, not_10_out, not_12_out, priority_encoder_1_gs, S0, S1, V0, V1, V2,
       V3, V4, V5, V6, V7, WriteL0, WriteL1, WriteL2, WriteL3, WriteL4, WriteL5, WriteL6, WriteL7;
  wire [1:0] controlled_buffer_25_out, \max2_归并比较_1_max_num , \max2_归并比较_2_max_num , \max2_归并比较_3_max_num ,
       priority_encoder_1_out;
  wire [12:0] Tag0, Tag1, Tag2, Tag3, Tag4, Tag5, Tag6, Tag7;
  wire [13:0] controlled_buffer_1_out, controlled_buffer_3_out, controlled_buffer_5_out,
       controlled_buffer_7_out;
  wire [15:0] C0, C1, C2, C3, C4, C5, C6, C7, controlled_buffer_13_out, controlled_buffer_14_out,
       controlled_buffer_15_out, controlled_buffer_16_out, \max2_归并比较_1_max , \max2_归并比较_2_max ;
  wire [31:0] controlled_buffer_27_out, register_1_q, register_2_q, register_3_q, register_4_q, register_5_q,
       register_6_q, register_7_q, register_8_q;

  Decoder #(.enable("false")) decoder_1 (.out0(S0), .out1(S1), .sel(not_1_out));
  not not_1 (not_1_out, Addr[2]);
  assign controlled_buffer_1_out = S0 ? {V0, Tag0} : 14'bz;  // Controlled_Buffer controlled_buffer_1
  assign controlled_buffer_1_out = S1 ? {V4, Tag4} : 14'bz;  // Controlled_Buffer controlled_buffer_2
  assign controlled_buffer_3_out = S0 ? {V1, Tag1} : 14'bz;  // Controlled_Buffer controlled_buffer_3
  assign controlled_buffer_3_out = S1 ? {V5, Tag5} : 14'bz;  // Controlled_Buffer controlled_buffer_4
  assign controlled_buffer_5_out = S0 ? {V2, Tag2} : 14'bz;  // Controlled_Buffer controlled_buffer_5
  assign controlled_buffer_5_out = S1 ? {V6, Tag6} : 14'bz;  // Controlled_Buffer controlled_buffer_6
  assign controlled_buffer_7_out = S0 ? {V3, Tag3} : 14'bz;  // Controlled_Buffer controlled_buffer_7
  assign controlled_buffer_7_out = S1 ? {V7, Tag7} : 14'bz;  // Controlled_Buffer controlled_buffer_8
  not not_2 (not_2_out, V7);
  not not_3 (not_3_out, V3);
  not not_4 (not_4_out, V6);
  not not_5 (not_5_out, V2);
  not not_6 (not_6_out, V5);
  not not_7 (not_7_out, V1);
  not not_8 (not_8_out, V4);
  not not_9 (not_9_out, V0);
  assign controlled_buffer_9_out = S0 ? not_3_out : 1'bz;  // Controlled_Buffer controlled_buffer_9
  assign controlled_buffer_10_out = S0 ? not_5_out : 1'bz;  // Controlled_Buffer controlled_buffer_10
  assign controlled_buffer_11_out = S0 ? not_7_out : 1'bz;  // Controlled_Buffer controlled_buffer_11
  assign controlled_buffer_12_out = S0 ? not_9_out : 1'bz;  // Controlled_Buffer controlled_buffer_12
  assign controlled_buffer_13_out = S0 ? C0 : 16'bz;  // Controlled_Buffer controlled_buffer_13
  assign controlled_buffer_14_out = S0 ? C1 : 16'bz;  // Controlled_Buffer controlled_buffer_14
  assign controlled_buffer_15_out = S0 ? C2 : 16'bz;  // Controlled_Buffer controlled_buffer_15
  assign controlled_buffer_16_out = S0 ? C3 : 16'bz;  // Controlled_Buffer controlled_buffer_16
  and and_1 (k0, controlled_buffer_1_out[13], comparator_1_eq);
  Comparator #(.width(13)) comparator_1 (
    .a(controlled_buffer_1_out[12:0]), .b(Addr[15:3]), .eq(comparator_1_eq));  // open: gt, lt
  and and_2 (k1, controlled_buffer_3_out[13], comparator_2_eq);
  Comparator #(.width(13)) comparator_2 (
    .a(controlled_buffer_3_out[12:0]), .b(Addr[15:3]), .eq(comparator_2_eq));  // open: gt, lt
  and and_3 (k2, controlled_buffer_5_out[13], comparator_3_eq);
  Comparator #(.width(13)) comparator_3 (
    .a(controlled_buffer_5_out[12:0]), .b(Addr[15:3]), .eq(comparator_3_eq));  // open: gt, lt
  and and_4 (k3, controlled_buffer_7_out[13], comparator_4_eq);
  Comparator #(.width(13)) comparator_4 (
    .a(controlled_buffer_7_out[12:0]), .b(Addr[15:3]), .eq(comparator_4_eq));  // open: gt, lt
  not not_10 (not_10_out, S0);
  assign controlled_buffer_9_out = not_10_out ? not_2_out : 1'bz;  // Controlled_Buffer controlled_buffer_17
  assign controlled_buffer_10_out = not_10_out ? not_4_out : 1'bz;  // Controlled_Buffer controlled_buffer_18
  assign controlled_buffer_11_out = not_10_out ? not_6_out : 1'bz;  // Controlled_Buffer controlled_buffer_19
  assign controlled_buffer_12_out = not_10_out ? not_8_out : 1'bz;  // Controlled_Buffer controlled_buffer_20
  assign controlled_buffer_13_out = not_10_out ? C4 : 16'bz;  // Controlled_Buffer controlled_buffer_21
  assign controlled_buffer_14_out = not_10_out ? C5 : 16'bz;  // Controlled_Buffer controlled_buffer_22
  assign controlled_buffer_15_out = not_10_out ? C6 : 16'bz;  // Controlled_Buffer controlled_buffer_23
  assign controlled_buffer_16_out = not_10_out ? C7 : 16'bz;  // Controlled_Buffer controlled_buffer_24
  \Max2_归并比较  \max2_归并比较_1  (
    .Y(controlled_buffer_14_out), .X(controlled_buffer_13_out), .Y_num(2'b10), .X_num(2'b11),
    .MAX(\max2_归并比较_1_max ), .MAX_num(\max2_归并比较_1_max_num ));
  \Max2_归并比较  \max2_归并比较_2  (
    .Y(controlled_buffer_16_out), .X(controlled_buffer_15_out), .Y_num(2'b00), .X_num(2'b01),
    .MAX(\max2_归并比较_2_max ), .MAX_num(\max2_归并比较_2_max_num ));
  or or_1 (Hit, k0, k1, k2, k3);
  Priority_Encoder #(.select(2)) priority_encoder_1 (
    .in0(controlled_buffer_9_out), .in1(controlled_buffer_10_out), .in2(controlled_buffer_11_out),
    .in3(controlled_buffer_12_out), .out(priority_encoder_1_out), .gs(priority_encoder_1_gs));  // open: en_out, en_in
  \Max2_归并比较  \max2_归并比较_3  (
    .Y(\max2_归并比较_2_max ), .X(\max2_归并比较_1_max ), .Y_num(\max2_归并比较_2_max_num ),
    .X_num(\max2_归并比较_1_max_num ), .MAX_num(\max2_归并比较_3_max_num ));  // open: MAX
  not not_11 (Miss, Hit);
  assign controlled_buffer_25_out = priority_encoder_1_gs ? priority_encoder_1_out : 2'bz;  // Controlled_Buffer controlled_buffer_25
  not not_12 (not_12_out, priority_encoder_1_gs);
  assign controlled_buffer_25_out = not_12_out ? \max2_归并比较_3_max_num  : 2'bz;  // Controlled_Buffer controlled_buffer_26
  and and_5 (L0, S0, k0);
  and and_6 (L1, S0, k1);
  and and_7 (L2, S0, k2);
  and and_8 (L3, S0, k3);
  and and_9 (L4, S1, k0);
  and and_10 (L5, S1, k1);
  and and_11 (L6, S1, k2);
  and and_12 (L7, S1, k3);
  Decoder #(.select(2), .disabled(0), .enable("false")) decoder_2 (
    .out0(Del3), .out1(Del2), .out2(Del1), .out3(Del0), .sel(controlled_buffer_25_out));
  Register #(.width(1)) VALID (.D(1'b1), .en(WriteL0), .Q(V0), .clk(CLK));  // open: clr
  Register #(.width(1)) VALID_2 (.D(1'b1), .en(WriteL1), .Q(V1), .clk(CLK));  // open: clr
  Register #(.width(1)) VALID_3 (.D(1'b1), .en(WriteL2), .Q(V2), .clk(CLK));  // open: clr
  Register #(.width(1)) VALID_4 (.D(1'b1), .en(WriteL3), .Q(V3), .clk(CLK));  // open: clr
  Register #(.width(1)) VALID_5 (.D(1'b1), .en(WriteL4), .Q(V4), .clk(CLK));  // open: clr
  Register #(.width(1)) VALID_6 (.D(1'b1), .en(WriteL5), .Q(V5), .clk(CLK));  // open: clr
  Register #(.width(1)) VALID_7 (.D(1'b1), .en(WriteL6), .Q(V6), .clk(CLK));  // open: clr
  Register #(.width(1)) VALID_8 (.D(1'b1), .en(WriteL7), .Q(V7), .clk(CLK));  // open: clr
  and and_13 (CWriteL0, S0, Del0);
  and and_14 (CWriteL1, S0, Del1);
  and and_15 (CWriteL2, S0, Del2);
  and and_16 (CWriteL3, S0, Del3);
  and and_17 (CWriteL4, S1, Del0);
  and and_18 (CWriteL5, S1, Del1);
  and and_19 (CWriteL6, S1, Del2);
  and and_20 (CWriteL7, S1, Del3);
  Register #(.width(13)) TAG (.D(Addr[15:3]), .en(WriteL0), .Q(Tag0), .clk(CLK));  // open: clr
  Register #(.width(13)) TAG_2 (.D(Addr[15:3]), .en(WriteL1), .Q(Tag1), .clk(CLK));  // open: clr
  Register #(.width(13)) TAG_3 (.D(Addr[15:3]), .en(WriteL2), .Q(Tag2), .clk(CLK));  // open: clr
  Register #(.width(13)) TAG_4 (.D(Addr[15:3]), .en(WriteL3), .Q(Tag3), .clk(CLK));  // open: clr
  Register #(.width(13)) TAG_5 (.D(Addr[15:3]), .en(WriteL4), .Q(Tag4), .clk(CLK));  // open: clr
  Register #(.width(13)) TAG_6 (.D(Addr[15:3]), .en(WriteL5), .Q(Tag5), .clk(CLK));  // open: clr
  Register #(.width(13)) TAG_7 (.D(Addr[15:3]), .en(WriteL6), .Q(Tag6), .clk(CLK));  // open: clr
  Register #(.width(13)) TAG_8 (.D(Addr[15:3]), .en(WriteL7), .Q(Tag7), .clk(CLK));  // open: clr
  Counter #(.width(16), .max('hffff)) \u_淘汰计数  (.count(1'b1), .Q(C0), .clk(CLK), .clr(L0));  // open: load, D, carry
  Counter #(.width(16), .max('hffff)) \u_淘汰计数_2  (.count(1'b1), .Q(C1), .clk(CLK), .clr(L1));  // open: load, D, carry
  Counter #(.width(16), .max('hffff)) \u_淘汰计数_3  (.count(1'b1), .Q(C2), .clk(CLK), .clr(L2));  // open: load, D, carry
  Counter #(.width(16), .max('hffff)) \u_淘汰计数_4  (.count(1'b1), .Q(C3), .clk(CLK), .clr(L3));  // open: load, D, carry
  Counter #(.width(16), .max('hffff)) \u_淘汰计数_5  (.count(1'b1), .Q(C4), .clk(CLK), .clr(L4));  // open: load, D, carry
  Counter #(.width(16), .max('hffff)) \u_淘汰计数_6  (.count(1'b1), .Q(C5), .clk(CLK), .clr(L5));  // open: load, D, carry
  Counter #(.width(16), .max('hffff)) \u_淘汰计数_7  (.count(1'b1), .Q(C6), .clk(CLK), .clr(L6));  // open: load, D, carry
  Counter #(.width(16), .max('hffff)) \u_淘汰计数_8  (.count(1'b1), .Q(C7), .clk(CLK), .clr(L7));  // open: load, D, carry
  and and_21 (WriteL7, BlkDataReady, CWriteL7);
  and and_22 (WriteL6, BlkDataReady, CWriteL6);
  and and_23 (WriteL5, BlkDataReady, CWriteL5);
  and and_24 (WriteL4, BlkDataReady, CWriteL4);
  and and_25 (WriteL3, BlkDataReady, CWriteL3);
  and and_26 (WriteL2, BlkDataReady, CWriteL2);
  and and_27 (WriteL1, BlkDataReady, CWriteL1);
  and and_28 (WriteL0, BlkDataReady, CWriteL0);
  assign controlled_buffer_27_out = L0 ? register_1_q : 32'bz;  // Controlled_Buffer controlled_buffer_27
  Register #(.width(32)) register_1 (.D(BlockDataIn), .en(WriteL0), .Q(register_1_q), .clk(CLK));  // open: clr
  Register #(.width(32)) register_2 (.D(BlockDataIn), .en(WriteL1), .Q(register_2_q), .clk(CLK));  // open: clr
  assign controlled_buffer_27_out = L1 ? register_2_q : 32'bz;  // Controlled_Buffer controlled_buffer_28
  Register #(.width(32)) register_3 (.D(BlockDataIn), .en(WriteL2), .Q(register_3_q), .clk(CLK));  // open: clr
  assign controlled_buffer_27_out = L2 ? register_3_q : 32'bz;  // Controlled_Buffer controlled_buffer_29
  Register #(.width(32)) register_4 (.D(BlockDataIn), .en(WriteL3), .Q(register_4_q), .clk(CLK));  // open: clr
  assign controlled_buffer_27_out = L3 ? register_4_q : 32'bz;  // Controlled_Buffer controlled_buffer_30
  Register #(.width(32)) register_5 (.D(BlockDataIn), .en(WriteL4), .Q(register_5_q), .clk(CLK));  // open: clr
  assign controlled_buffer_27_out = L4 ? register_5_q : 32'bz;  // Controlled_Buffer controlled_buffer_31
  assign controlled_buffer_27_out = L5 ? register_6_q : 32'bz;  // Controlled_Buffer controlled_buffer_32
  Register #(.width(32)) register_6 (.D(BlockDataIn), .en(WriteL5), .Q(register_6_q), .clk(CLK));  // open: clr
  assign controlled_buffer_27_out = L6 ? register_7_q : 32'bz;  // Controlled_Buffer controlled_buffer_33
  Register #(.width(32)) register_7 (.D(BlockDataIn), .en(WriteL6), .Q(register_7_q), .clk(CLK));  // open: clr
  assign controlled_buffer_27_out = L7 ? register_8_q : 32'bz;  // Controlled_Buffer controlled_buffer_34
  Register #(.width(32)) register_8 (.D(BlockDataIn), .en(WriteL7), .Q(register_8_q), .clk(CLK));  // open: clr
  Multiplexer #(.select(2), .width(8)) multiplexer_1 (
    .in0(controlled_buffer_27_out[7:0]), .in1(controlled_buffer_27_out[15:8]),
    .in2(controlled_buffer_27_out[23:16]), .in3(controlled_buffer_27_out[31:24]), .out(DataOut),
    .sel(Addr[1:0]), .en(Hit));

  // Other names for the same wires on the sheet: Blk[31:0] = BlockDataIn; BlkReady = BlkDataReady;
  //   OFFSET[1:0] = Addr[1:0]; 字节地址[15:0] = Addr; INDEX = Addr[2]; Tag[12:0] = Addr[15:3]

  // Notes on the sheet:
  //   输入引脚区
  //   请勿增改引脚，请勿修改子电路封装
  //   电路功能：利用上面给定的隧道构建8行的Cache，cache映射方式自选
  //   请在下方利用上方输入输出引脚的隧道信号构建电路，ctrl+d复制选择部件
  //   输出引脚区
endmodule

module \Cache自动测试  (
);

  wire and_2_out, Clk, comparator_1_lt, comparator_2_eq, EN, Hit, Miss, RDY, Runing;
  wire [3:0] _1, _2, _3;
  wire [7:0] Dataout, rom_2_data;
  wire [15:0] adder_1_out, bit_extender_3_out, \cache块交换_1_byteaddrout , counter_1_q, rom_1_data,
       subtractor_1_out, \实际命中 , \时钟周期数 , \校验和 , \缺失次数 , \计数器_q , \访问次数 ;
  wire [31:0] bit_extender_1_out, bit_extender_2_out, \cache块交换_1_blockdatain , divider_1_out, divider_2_out,
       multiplier_1_out;
  wire [31:4] divider_2_rem, divider_3_out, divider_3_rem;

  Clock clock_1 (.out(Clk));
  // Probe on \实际命中 
  // Probe on \时钟周期数 
  not not_1 (Hit, Miss);
  Counter #(.width(16), .max('hffff)) \u_计数器  (.count(EN), .Q(\计数器_q ), .clk(Clk));  // open: load, D, carry, clr
  and and_1 (EN, Hit, Runing);
  and and_2 (and_2_out, Miss, RDY, Runing);
  // Probe on \计数器_q 
  Counter #(.width(16), .max('hffff)) counter_1 (
    .count(and_2_out), .Q(counter_1_q), .clk(Clk));  // open: load, D, carry, clr
  Subtractor #(.width(16)) subtractor_1 (.a(\访问次数 ), .b(\缺失次数 ), .out(subtractor_1_out));  // open: bin, bout
  Comparator #(.width(16)) comparator_1 (.a(\访问次数 ), .b(\缺失次数 ), .lt(comparator_1_lt));  // open: gt, eq
  Comparator #(.width(16)) comparator_2 (.a(\计数器_q ), .b(16'h100), .eq(comparator_2_eq));  // open: gt, lt
  not not_2 (Runing, comparator_2_eq);
  Register #(.width(16)) register_1 (.D(counter_1_q), .en(EN), .Q(\缺失次数 ), .clk(Clk));  // open: clr
  Multiplexer #(.width(16), .disabled(0), .enable("false")) multiplexer_1 (
    .in0(subtractor_1_out), .in1({16{1'b0}}), .out(\实际命中 ), .sel(comparator_1_lt));
  // Probe on \缺失次数 
  // Probe on \校验和 
  ROM #(.addrWidth(16), .dataWidth(16)) rom_1 (.addr(\计数器_q ), .data(rom_1_data));  // open: sel
  Counter #(.width(16), .max('hffff)) counter_2 (.count(EN), .Q(\访问次数 ), .clk(Clk));  // open: load, D, carry, clr
  assign bit_extender_1_out = {{16{1'b0}}, \实际命中 };  // Bit_Extender bit_extender_1
  // Probe on \访问次数 
  \Cache_4路组相联  \cache_4路组相联_1  (
    .BlockDataIn(\cache块交换_1_blockdatain ), .Addr(rom_1_data), .BlkDataReady(RDY), .CLK(Clk), .Miss(Miss),
    .DataOut(Dataout));
  Counter #(.width(16), .max('hffff)) counter_3 (.count(Runing), .Q(\时钟周期数 ), .clk(Clk));  // open: load, D, carry, clr
  Multiplier #(.width(32)) multiplier_1 (
    .a(bit_extender_1_out), .b(32'h64), .out(multiplier_1_out));  // open: cin, cout
  assign bit_extender_2_out = {{16{1'b0}}, \访问次数 };  // Bit_Extender bit_extender_2
  Divider #(.width(32)) divider_1 (
    .a(multiplier_1_out), .b(bit_extender_2_out), .out(divider_1_out));  // open: upper, rem
  Pull_Resistor #(.pull(1)) pull_resistor_1 (.node(Miss));
  LED \u_缺失  (.in(Miss));
  Hex_Digit_Display hex_digit_display_1 (.value(_3), .dp(1'b1));
  \Cache块交换  \cache块交换_1  (
    .Addr(rom_1_data), .CLK(Clk), .ByteAddrOut(\cache块交换_1_byteaddrout ), .ByteDataIn(rom_2_data),
    .Miss(Miss), .BlkDataReady(RDY), .BlockDataIn(\cache块交换_1_blockdatain ), .Enable(Runing));
  assign bit_extender_3_out = {{8{1'b0}}, Dataout};  // Bit_Extender bit_extender_3
  Divider #(.width(32)) divider_2 (
    .a(divider_1_out), .b(32'ha), .out(divider_2_out), .rem({divider_2_rem, _1}));  // open: upper
  Hex_Digit_Display hex_digit_display_2 (.value(_1));  // open: dp
  Hex_Digit_Display hex_digit_display_3 (.value(_2));  // open: dp
  Adder #(.width(16)) adder_1 (.a(\校验和 ), .b(bit_extender_3_out), .out(adder_1_out));  // open: cin, cout
  Divider #(.width(32)) divider_3 (
    .a(divider_2_out), .b(32'ha), .out({divider_3_out, _3}), .rem({divider_3_rem, _2}));  // open: upper
  ROM #(.addrWidth(16)) rom_2 (.addr(\cache块交换_1_byteaddrout ), .data(rom_2_data));  // open: sel
  Register #(.width(16)) \u_校验和  (.D(adder_1_out), .en(EN), .Q(\校验和 ), .clk(Clk));  // open: clr

  // Notes on the sheet:
  //   ctrl+r复位
  //   Trace存储器
  //   电路功能：测试Cache模块， ctrl+k启动时钟后，会自动对cache模块进行读数据测试，并将数据逐一读出进行校验和计算
  //   contents of rom_1 (hex, n*v repeats v):
  //   0 1 2 3 8 9 a b 10 11 12 13 20 21 22 23 8 9 a b 4 5 6 7 24 25 26 27 4 5 6 7 0 1 2 3 8 9 a b 8 9 a b
  //   20 21 22 23 28 29 2a 2b 24 25 26 27 4 5 6 7 24 25 26 27 0 1 2 3 8 9 a b 20 21 22 23 20 21 22 23 30
  //   31 32 33 4 5 6 7 24 25 26 27 4 5 6 7 0 1 2 3 8 9 a b 20 21 22 23 20 21 22 23 28 29 2a 2b 4 5 6 7 24
  //   2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
  //   如果设计了不同的映射方式，可以将该电路中cache模块替换为对应Cache模块即可!
  //   参数统计区
  //   命中率
  //   电路状态稳定后显示最终命中率
  //   二级存储器
  //   Cache模拟器
  //   contents of rom_2 (hex, n*v repeats v):
  //   0 1 2 3 4 5 6 7 8 9 a b c d e f 10 11 12 13 14 15 16 17 18 19 1a 1b 1c 1d 1e 1f 20 21 22 23 24 25 26
  //   27 28 29 2a 2b 2c 2d 2e 2f 30 31 32 33 34 35 36 37 38 39 3a 3b 3c 3d 3e 3f 40 41 42 43 44 45 46 47
  //   48 49 4a 4b 4c 4d 4e 4f 50 51 52 53 54 55 56 57 58 59 5a 5b 5c 5d 5e 5f 60 61 62 63 64 65 66 67 68 6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
endmodule

// Max2
module \Max2_归并比较  (
  input  [15:0] Y,
  input  [15:0] X,
  input  [1:0] Y_num,
  input  [1:0] X_num,
  output [15:0] MAX,
  output [1:0] MAX_num
);

  wire comparator_1_eq, comparator_1_gt, or_1_out;

  Multiplexer #(.width(16)) multiplexer_1 (.in0(Y), .in1(X), .out(MAX), .sel(or_1_out), .en(1'b1));
  Comparator #(.width(16), .mode("unsigned")) comparator_1 (
    .a(X), .b(Y), .gt(comparator_1_gt), .eq(comparator_1_eq));  // open: lt
  or or_1 (or_1_out, comparator_1_gt, comparator_1_eq);
  Multiplexer #(.width(2), .enable("false")) multiplexer_2 (.in0(Y_num), .in1(X_num), .out(MAX_num), .sel(or_1_out));

  // Notes on the sheet:
  //   输出两个输入中的较大值，并输出较大值的2位编号
endmodule

// Max3
module \Max3_归并比较  (
  input  [15:0] Y,
  input  [15:0] X,
  input  [2:0] Y_num,
  input  [2:0] X_num,
  output [15:0] MAX,
  output [2:0] Max_num
);

  wire comparator_1_eq, comparator_1_gt, or_1_out;

  Multiplexer #(.width(16), .enable("false")) multiplexer_1 (.in0(Y), .in1(X), .out(MAX), .sel(or_1_out));
  Comparator #(.width(16), .mode("unsigned")) comparator_1 (
    .a(X), .b(Y), .gt(comparator_1_gt), .eq(comparator_1_eq));  // open: lt
  or or_1 (or_1_out, comparator_1_gt, comparator_1_eq);
  Multiplexer #(.width(3), .enable("false")) multiplexer_2 (.in0(Y_num), .in1(X_num), .out(Max_num), .sel(or_1_out));

  // Notes on the sheet:
  //   输出两个输入中的较大值，并输出较大值的3位编号
endmodule

module \Cache块交换  (
  input  [15:0] Addr,
  input  [7:0] ByteDataIn,
  input  Miss,
  input  Enable,
  input  CLK,
  output [15:0] ByteAddrOut,
  output [31:0] BlockDataIn,
  output BlkDataReady
);

  wire \块交换状态机_1_byte0_ready , \块交换状态机_1_byte1_ready , \块交换状态机_1_byte2_ready , \块交换状态机_1_byte3_ready ;
  wire [7:0] register_1_q, register_2_q, register_3_q, register_4_q;

  assign ByteAddrOut = \块交换状态机_1_byte0_ready  ? {Addr[15:2], 2'b00} : 16'bz;  // Controlled_Buffer controlled_buffer_1
  \块交换状态机  \u_块交换状态机_1  (
    .Clk(CLK), .Miss(Miss), .Byte0_Ready(\块交换状态机_1_byte0_ready ), .Byte1_Ready(\块交换状态机_1_byte1_ready ),
    .Byte2_Ready(\块交换状态机_1_byte2_ready ), .Byte3_Ready(\块交换状态机_1_byte3_ready ), .Byte0_Ready_2(BlkDataReady),
    .En(Enable));
  assign ByteAddrOut = \块交换状态机_1_byte1_ready  ? {Addr[15:2], 2'b01} : 16'bz;  // Controlled_Buffer controlled_buffer_2
  assign ByteAddrOut = \块交换状态机_1_byte2_ready  ? {Addr[15:2], 2'b10} : 16'bz;  // Controlled_Buffer controlled_buffer_3
  assign ByteAddrOut = \块交换状态机_1_byte3_ready  ? {Addr[15:2], 2'b11} : 16'bz;  // Controlled_Buffer controlled_buffer_4
  Register register_1 (.D(ByteDataIn), .en(\块交换状态机_1_byte0_ready ), .Q(register_1_q), .clk(CLK));  // open: clr
  Register register_2 (.D(ByteDataIn), .en(\块交换状态机_1_byte1_ready ), .Q(register_2_q), .clk(CLK));  // open: clr
  Register register_3 (.D(ByteDataIn), .en(\块交换状态机_1_byte2_ready ), .Q(register_3_q), .clk(CLK));  // open: clr
  Register register_4 (.D(ByteDataIn), .en(\块交换状态机_1_byte3_ready ), .Q(register_4_q), .clk(CLK));  // open: clr
  assign BlockDataIn = BlkDataReady ? {register_4_q, register_3_q, register_2_q, register_1_q} : 32'bz;  // Controlled_Buffer controlled_buffer_5

  // Notes on the sheet:
  //   数据缓存寄存器
endmodule

// 状态机
module \块交换状态机  (
  input  En,
  input  Clk,
  input  Miss,
  output Byte0_Ready,
  output Byte1_Ready,
  output Byte2_Ready,
  output Byte3_Ready,
  output Byte0_Ready_2
);

  wire and_1_out, and_2_out, and_3_out, and_4_out, and_5_out, and_6_out, and_7_out, Next_Q0, Next_Q1,
       Next_Q2, Next_Q3, not_1_out, not_2_out, not_3_out, not_4_out, not_5_out, not_6_out, not_7_out,
       not_8_out, not_9_out, not_10_out, not_11_out, not_12_out, not_13_out, or_1_out, or_2_out, Q0, Q1, Q2,
       Q3;

  not not_1 (not_1_out, Q3);
  not not_2 (not_2_out, Q3);
  not not_3 (not_3_out, Q2);
  not not_4 (not_4_out, Q3);
  not not_5 (not_5_out, Q1);
  not not_6 (not_6_out, Q3);
  not not_7 (not_7_out, Q0);
  not not_8 (not_8_out, Q3);
  not not_9 (not_9_out, Q0);
  D_Flip_Flop d_ff_1 (.clk(Clk), .D(Next_Q3), .Q(Q3), .en(En));  // open: Qn, preset, reset
  D_Flip_Flop d_ff_2 (.clk(Clk), .D(Next_Q2), .Q(Q2), .en(En));  // open: Qn, preset, reset
  D_Flip_Flop d_ff_3 (.clk(Clk), .D(Next_Q1), .Q(Q1), .en(En));  // open: Qn, preset, reset
  D_Flip_Flop d_ff_4 (.clk(Clk), .D(Next_Q0), .Q(Q0), .en(En));  // open: Qn, preset, reset
  and and_1 (and_1_out, not_1_out, Q2, Q1, Q0);
  and and_2 (and_2_out, not_2_out, not_3_out, Q1, Q0);
  not not_10 (not_10_out, Q3);
  and and_3 (and_3_out, not_10_out, Q2, not_11_out);
  not not_11 (not_11_out, Q1);
  not not_12 (not_12_out, Q3);
  and and_4 (and_4_out, not_12_out, Q2, not_13_out);
  not not_13 (not_13_out, Q0);
  and and_5 (and_5_out, not_4_out, not_5_out, Q0);
  and and_6 (and_6_out, not_6_out, Q1, not_7_out);
  and and_7 (and_7_out, not_8_out, not_9_out);
  or or_1 (or_1_out, and_2_out, and_3_out, and_4_out);
  or or_2 (or_2_out, and_5_out, and_6_out);
  Decoder #(.select(4), .disabled(0), .enable("false")) decoder_1 (
    .out1(Byte0_Ready), .out3(Byte1_Ready), .out5(Byte2_Ready), .out7(Byte3_Ready), .out8(Byte0_Ready_2),
    .sel({Q3, Q2, Q1, Q0}));  // open: out0, out2, out4, out6, out9, out10, out11, out12, out13, out14, out15
  and and_8 (Next_Q3, and_1_out, Miss);
  and and_9 (Next_Q2, or_1_out, Miss);
  and and_10 (Next_Q1, Miss, or_2_out);
  and and_11 (Next_Q0, Miss, and_7_out);
endmodule

// 评分
module \Regfile评分逻辑  (
  input  EQ,
  input  EN,
  input  CLK,
  output [31:0] \正确条数 ,
  output [3:0] High,
  output [3:0] Low,
  output [3:0] Mid,
  output [31:0] Total,
  output Right
);

  wire and_1_out, priority_encoder_1_gs, priority_encoder_1_out;
  wire [31:0] divider_1_out, divider_2_out, multiplier_1_out;
  wire [31:4] divider_2_rem, divider_3_out, divider_3_rem;

  Counter #(.width(32), .max('hffffffff)) counter_1 (.count(EN), .Q(Total), .clk(CLK));  // open: load, D, carry, clr
  Priority_Encoder #(.select(1)) priority_encoder_1 (
    .in0(EQ), .in1(EQ), .out(priority_encoder_1_out), .gs(priority_encoder_1_gs));  // open: en_out, en_in
  and and_1 (and_1_out, priority_encoder_1_out, priority_encoder_1_gs, EN);
  Counter #(.width(32), .max('hffffffff)) counter_2 (
    .count(and_1_out), .Q(\正确条数 ), .clk(CLK));  // open: load, D, carry, clr
  Multiplier #(.width(32)) multiplier_1 (.a(\正确条数 ), .b(32'h64), .out(multiplier_1_out));  // open: cin, cout
  Divider #(.width(32)) divider_1 (.a(multiplier_1_out), .b(Total), .out(divider_1_out));  // open: upper, rem
  Comparator #(.width(32)) comparator_1 (.a(\正确条数 ), .b(Total), .eq(Right));  // open: gt, lt
  Divider #(.width(32)) divider_2 (
    .a(divider_1_out), .b(32'ha), .out(divider_2_out), .rem({divider_2_rem, Low}));  // open: upper
  Divider #(.width(32)) divider_3 (
    .a(divider_2_out), .b(32'ha), .out({divider_3_out, High}), .rem({divider_3_rem, Mid}));  // open: upper

  // Notes on the sheet:
  //   只有使用优先编码器才能屏蔽掉位置状态
endmodule
